// Logisim project BasicComputer.circ as structural Verilog: 27 circuits, main circuit BasicComputer
module main (
  input  ENABLE,
  input  [7:0] in_2,
  input  in_3,
  output [7:0] out_4
);

  wire AC_p1, CLOCK, S_MUX_CS;
  wire [1:0] AB_CS, Memory_CS;
  wire [2:0] DB_CS;
  wire [3:0] AC_CS, AR_CS, GPRA_CS, GPRB_CS, INPR_CS, IR_CS, OUTR_CS, PC_CS, SP_CS, X_CS;
  wire [4:0] X;
  wire [7:0] bit_extender_3_out, INPR;
  wire [9:0] ABUS, adder_1_out, AR, AR_IN, bit_extender_1_out, bit_extender_2_out, bit_extender_7_out,
       bit_extender_8_out, bit_extender_9_out, PC, SP;
  wire [15:0] AC, ALU_BUS, bit_extender_4_out, bit_extender_5_out, bit_extender_6_out, DBUS, GPRA, GPRB, IR,
       Memory;

  Bit_Extender #(.in_width(16), .out_width(10)) bit_extender_1 (.in(DBUS), .out(bit_extender_1_out));
  Bit_Extender #(.in_width(16), .out_width(10)) bit_extender_2 (.in(DBUS), .out(bit_extender_2_out));
  // _10_Bit_Register PC: pin names not known; wires that end beside it: bit_extender_1_out, ENABLE, CLOCK, PC_CS, PC
  // _10_Bit_Register AR: pin names not known; wires that end beside it: AR_IN, ENABLE, CLOCK, AR_CS, AR
  // _10_Bit_Register SP: pin names not known; wires that end beside it: bit_extender_2_out, ENABLE, CLOCK, SP_CS, SP
  RAM #(.addrWidth(10), .dataWidth(16), .bus("separate")) ram_1 (
    .addr(ABUS), .din(DBUS), .data(Memory), .str(Memory_CS[1]), .sel(ENABLE), .ld(Memory_CS[0]));  // open: clk, clr
  // _16_Bit_Register GPRB: pin names not known; wires that end beside it: DBUS, ENABLE, CLOCK, GPRB_CS, GPRB
  // _16_Bit_Register AC: pin names not known; wires that end beside it: AC_p1, ENABLE, CLOCK, AC_CS, AC
  // _16_Bit_Register IR: pin names not known; wires that end beside it: DBUS, ENABLE, CLOCK, IR_CS, IR
  // _16_Bit_Register GPRA: pin names not known; wires that end beside it: DBUS, ENABLE, CLOCK, GPRA_CS, GPRA
  Bit_Extender #(.in_width(16), .out_width(8)) bit_extender_3 (.in(DBUS), .out(bit_extender_3_out));
  // _5_Bit_Register X: pin names not known; wires that end beside it: ENABLE, CLOCK, X_CS, X
  // _8_Bit_Register INPR: pin names not known; wires that end beside it: in_2, ENABLE, CLOCK, INPR_CS, INPR
  // _8_Bit_Register OUTR: pin names not known; wires that end beside it: bit_extender_3_out, ENABLE, CLOCK, OUTR_CS, out_4
  ControlUnit controlunit_1 (
    .Enable(ENABLE), .in_2(IR), .out_4(AB_CS), .out_7(AR_CS), .out_8(IR_CS), .out_9(PC_CS),
    .out_10(Memory_CS), .out_5(DB_CS), .in_3(CLOCK), .out_6(S_MUX_CS));
  Clock clock_1 (.out(CLOCK));
  assign bit_extender_4_out = {{6{1'b0}}, ABUS};  // Bit_Extender bit_extender_4
  assign bit_extender_5_out = {{11{1'b0}}, X};  // Bit_Extender bit_extender_5
  assign bit_extender_6_out = {{8{1'b0}}, INPR};  // Bit_Extender bit_extender_6
  Bit_Extender #(.in_width(16), .out_width(10)) bit_extender_7 (.in(IR), .out(bit_extender_7_out));
  Bit_Extender #(.in_width(16), .out_width(10)) bit_extender_8 (.in(DBUS), .out(bit_extender_8_out));
  Adder #(.width(10)) adder_1 (.a(bit_extender_8_out), .b(bit_extender_9_out), .out(adder_1_out));  // open: cin, cout
  assign bit_extender_9_out = {{5{1'b0}}, X};  // Bit_Extender bit_extender_9
  Multiplexer #(.select(2), .width(10)) multiplexer_1 (
    .in0(PC), .in1(AR), .in2(SP), .in3(SP), .out(ABUS), .sel(AB_CS), .en(ENABLE));
  Multiplexer #(.select(3), .width(16)) multiplexer_2 (
    .in0(Memory), .in1(bit_extender_4_out), .in2(GPRB), .in3(AC), .in4(GPRA), .in5(bit_extender_5_out),
    .in6(bit_extender_6_out), .in7(IR), .out(DBUS), .sel(DB_CS), .en(ENABLE));
  Multiplexer #(.width(10)) multiplexer_3 (
    .in0(bit_extender_7_out), .in1(adder_1_out), .out(AR_IN), .sel(S_MUX_CS), .en(ENABLE));
  Multiplexer #(.width(16)) multiplexer_4 (.in0(GPRA), .in1(GPRB), .out(ALU_BUS), .sel(in_3), .en(ENABLE));
endmodule

module _1_Bit_Register (
  input  in_1,
  input  in_2,
  input  in_3,
  input  in_4,
  input  [2:0] in_5,
  output out_6,
  output out_7
);

  wire and_2_out, and_3_out, multiplexer_1_out, not_1_out, not_2_out, not_3_out, xor_1_out;
  wire [1:0] or_1_out;

  xor xor_1 (xor_1_out, in_3, out_6);
  not not_1 (not_1_out, in_5[0]);
  not not_2 (not_2_out, in_5[1]);
  and and_1 (or_1_out[1], not_2_out, not_3_out);
  not not_3 (not_3_out, in_5[2]);
  and and_2 (and_2_out, not_1_out, not_3_out);
  and and_3 (and_3_out, not_3_out, in_5[1]);
  Multiplexer #(.select(2)) multiplexer_1 (
    .in0(in_2), .in1(xor_1_out), .in2(1'b0), .out(multiplexer_1_out), .sel(or_1_out), .en(in_4));  // open: in3
  or or_1 (or_1_out[0], and_2_out, and_3_out);
  D_Flip_Flop d_ff_1 (.clk(in_1), .D(multiplexer_1_out), .Q(out_6), .en(in_4));  // open: Qn, preset, reset
  and and_4 (out_7, out_6, in_3);
endmodule

module _4_Bit_Register (
  input  in_1,
  input  [3:0] in_2,
  input  [2:0] in_3,
  input  in_4,
  input  in_5,
  output out_6,
  output [3:0] out_7
);

  wire n1_bit_register_2_out_7, n1_bit_register_3_out_7, n1_bit_register_4_out_7;

  _1_Bit_Register u_1_bit_register_1 (
    .in_2(in_2[3]), .in_3(n1_bit_register_2_out_7), .out_6(out_7[3]), .in_4(in_4), .out_7(out_6),
    .in_5(in_3), .in_1(in_1));
  _1_Bit_Register u_1_bit_register_2 (
    .in_2(in_2[2]), .in_3(n1_bit_register_3_out_7), .out_6(out_7[2]), .in_4(in_4),
    .out_7(n1_bit_register_2_out_7), .in_5(in_3), .in_1(in_1));
  _1_Bit_Register u_1_bit_register_3 (
    .in_2(in_2[1]), .in_3(n1_bit_register_4_out_7), .out_6(out_7[1]), .in_4(in_4),
    .out_7(n1_bit_register_3_out_7), .in_5(in_3), .in_1(in_1));
  _1_Bit_Register u_1_bit_register_4 (
    .in_2(in_2[0]), .in_3(in_5), .out_6(out_7[0]), .in_4(in_4), .out_7(n1_bit_register_4_out_7), .in_5(in_3),
    .in_1(in_1));
endmodule

module _5_Bit_Register (
  input  in_1,
  input  [4:0] in_2,
  input  in_3,
  input  [2:0] in_4,
  output out_5,
  output [4:0] out_6
);

  wire n4_bit_register_1_out_6;

  _1_Bit_Register u_1_bit_register_1 (
    .in_2(in_2[4]), .in_3(n4_bit_register_1_out_6), .out_6(out_6[4]), .in_4(in_3), .out_7(out_5),
    .in_5(in_4), .in_1(in_1));
  _4_Bit_Register u_4_bit_register_1 (
    .out_6(n4_bit_register_1_out_6), .out_7(out_6[3:0]), .in_2(in_2[3:0]), .in_4(in_3), .in_3(in_4),
    .in_5(1'b1), .in_1(in_1));
endmodule

module _8_Bit_Register (
  input  in_1,
  input  [7:0] in_2,
  input  in_3,
  input  [2:0] in_4,
  output out_5,
  output [7:0] out_6
);

  wire n4_bit_register_2_out_6;

  _4_Bit_Register u_4_bit_register_1 (
    .out_6(out_5), .out_7(out_6[7:4]), .in_2(in_2[7:4]), .in_4(in_3), .in_3(in_4),
    .in_5(n4_bit_register_2_out_6), .in_1(in_1));
  _4_Bit_Register u_4_bit_register_2 (
    .out_6(n4_bit_register_2_out_6), .out_7(out_6[3:0]), .in_2(in_2[3:0]), .in_4(in_3), .in_3(in_4),
    .in_5(1'b1), .in_1(in_1));
endmodule

module _10_Bit_Register (
  input  in_1,
  input  [9:0] in_2,
  input  [2:0] in_3,
  input  in_4,
  output out_5,
  output [9:0] out_6
);

  wire n1_bit_register_2_out_7, n4_bit_register_1_out_6, n4_bit_register_2_out_6;

  _1_Bit_Register u_1_bit_register_1 (
    .in_2(in_2[9]), .in_3(n1_bit_register_2_out_7), .out_6(out_6[9]), .in_4(in_4), .out_7(out_5),
    .in_5(in_3), .in_1(in_1));
  _1_Bit_Register u_1_bit_register_2 (
    .in_2(in_2[8]), .in_3(n4_bit_register_1_out_6), .out_6(out_6[8]), .in_4(in_4),
    .out_7(n1_bit_register_2_out_7), .in_5(in_3), .in_1(in_1));
  _4_Bit_Register u_4_bit_register_1 (
    .out_6(n4_bit_register_1_out_6), .out_7(out_6[7:4]), .in_2(in_2[7:4]), .in_4(in_4), .in_3(in_3),
    .in_5(n4_bit_register_2_out_6), .in_1(in_1));
  _4_Bit_Register u_4_bit_register_2 (
    .out_6(n4_bit_register_2_out_6), .out_7(out_6[3:0]), .in_2(in_2[3:0]), .in_4(in_4), .in_3(in_3),
    .in_5(1'b1), .in_1(in_1));
endmodule

module _12_Bit_Register (
  input  in_1,
  input  [11:0] in_2,
  input  in_3,
  input  [2:0] in_4,
  output out_5,
  output [11:0] out_6
);

  wire n4_bit_register_2_out_6, n4_bit_register_3_out_6;

  _4_Bit_Register u_4_bit_register_1 (
    .out_6(out_5), .out_7(out_6[11:8]), .in_2(in_2[11:8]), .in_4(in_3), .in_3(in_4),
    .in_5(n4_bit_register_2_out_6), .in_1(in_1));
  _4_Bit_Register u_4_bit_register_2 (
    .out_6(n4_bit_register_2_out_6), .out_7(out_6[7:4]), .in_2(in_2[7:4]), .in_4(in_3), .in_3(in_4),
    .in_5(n4_bit_register_3_out_6), .in_1(in_1));
  _4_Bit_Register u_4_bit_register_3 (
    .out_6(n4_bit_register_3_out_6), .out_7(out_6[3:0]), .in_2(in_2[3:0]), .in_4(in_3), .in_3(in_4),
    .in_5(1'b1), .in_1(in_1));
endmodule

module _16_Bit_Register (
  input  in_1,
  input  [15:0] in_2,
  input  in_3,
  input  [2:0] in_4,
  output out_5,
  output [15:0] out_6
);

  wire n4_bit_register_2_out_6, n4_bit_register_3_out_6, n4_bit_register_4_out_6;

  _4_Bit_Register u_4_bit_register_1 (
    .out_6(out_5), .out_7(out_6[15:12]), .in_2(in_2[15:12]), .in_4(in_3), .in_3(in_4),
    .in_5(n4_bit_register_2_out_6), .in_1(in_1));
  _4_Bit_Register u_4_bit_register_2 (
    .out_6(n4_bit_register_2_out_6), .out_7(out_6[11:8]), .in_2(in_2[11:8]), .in_4(in_3), .in_3(in_4),
    .in_5(n4_bit_register_3_out_6), .in_1(in_1));
  _4_Bit_Register u_4_bit_register_3 (
    .out_6(n4_bit_register_3_out_6), .out_7(out_6[7:4]), .in_2(in_2[7:4]), .in_4(in_3), .in_3(in_4),
    .in_5(n4_bit_register_4_out_6), .in_1(in_1));
  _4_Bit_Register u_4_bit_register_4 (
    .out_6(n4_bit_register_4_out_6), .out_7(out_6[3:0]), .in_2(in_2[3:0]), .in_4(in_3), .in_3(in_4),
    .in_5(1'b1), .in_1(in_1));
endmodule

module Half_Adder (
  input  X,
  input  Y,
  output S,
  output C
);

  xor xor_1 (S, X, Y);
  and and_1 (C, X, Y);
endmodule

module Full_Adder (
  input  in_1,
  input  in_2,
  input  in_3,
  output out_4,
  output out_5
);

  wire half_adder_1_c, half_adder_1_s, half_adder_2_c;

  Half_Adder half_adder_1 (.X(in_1), .Y(in_2), .S(half_adder_1_s), .C(half_adder_1_c));
  Half_Adder half_adder_2 (.X(half_adder_1_s), .Y(in_3), .S(out_4), .C(half_adder_2_c));
  or or_1 (out_5, half_adder_2_c, half_adder_1_c);
endmodule

module _1_Bit_AU (
  input  in_1,
  input  in_2,
  input  in_3,
  input  [1:0] in_4,
  input  in_5,
  output out_6,
  output out_7
);

  wire multiplexer_1_out, not_1_out, not_2_out;

  not not_1 (not_1_out, in_2);
  not not_2 (not_2_out, 1'b0);
  Multiplexer #(.select(2)) multiplexer_1 (
    .in0(1'b0), .in1(in_2), .in2(not_1_out), .in3(not_2_out), .out(multiplexer_1_out), .sel(in_4), .en(in_3));
  Adder #(.width(1)) adder_1 (.a(in_1), .b(multiplexer_1_out), .out(out_6), .cin(in_5), .cout(out_7));
endmodule

module _4_Bit_AU (
  input  [3:0] in_1,
  input  in_2,
  input  in_3,
  input  [1:0] in_4,
  input  [3:0] in_5,
  output [3:0] out_6,
  output out_7
);

  wire n1_bit_au_2_out_7, n1_bit_au_3_out_7, n1_bit_au_4_out_7;

  _1_Bit_AU u_1_bit_au_1 (
    .in_1(in_1[3]), .in_2(in_5[3]), .out_6(out_6[3]), .out_7(out_7), .in_3(in_2), .in_4(in_4),
    .in_5(n1_bit_au_2_out_7));
  _1_Bit_AU u_1_bit_au_2 (
    .in_1(in_1[2]), .in_2(in_5[2]), .out_6(out_6[2]), .out_7(n1_bit_au_2_out_7), .in_3(in_2), .in_4(in_4),
    .in_5(n1_bit_au_3_out_7));
  _1_Bit_AU u_1_bit_au_3 (
    .in_1(in_1[1]), .in_2(in_5[1]), .out_6(out_6[1]), .out_7(n1_bit_au_3_out_7), .in_3(in_2), .in_4(in_4),
    .in_5(n1_bit_au_4_out_7));
  _1_Bit_AU u_1_bit_au_4 (
    .in_1(in_1[0]), .in_2(in_5[0]), .out_6(out_6[0]), .out_7(n1_bit_au_4_out_7), .in_3(in_2), .in_4(in_4),
    .in_5(in_3));
endmodule

module _16_Bit_AU (
  input  [15:0] in_1,
  input  in_2,
  input  [1:0] in_3,
  input  in_4,
  input  [15:0] in_5,
  output [15:0] out_6,
  output out_7
);

  wire n4_bit_au_2_out_7, n4_bit_au_3_out_7, n4_bit_au_4_out_7;

  _4_Bit_AU u_4_bit_au_1 (
    .in_1(in_1[15:12]), .in_2(in_2), .in_3(n4_bit_au_2_out_7), .in_5(in_5[15:12]), .out_7(out_7),
    .in_4(in_3), .out_6(out_6[15:12]));
  _4_Bit_AU u_4_bit_au_2 (
    .in_1(in_1[11:8]), .in_2(in_2), .in_3(n4_bit_au_3_out_7), .in_5(in_5[11:8]), .out_7(n4_bit_au_2_out_7),
    .in_4(in_3), .out_6(out_6[11:8]));
  _4_Bit_AU u_4_bit_au_3 (
    .in_1(in_1[7:4]), .in_2(in_2), .in_3(n4_bit_au_4_out_7), .in_5(in_5[7:4]), .out_7(n4_bit_au_3_out_7),
    .in_4(in_3), .out_6(out_6[7:4]));
  _4_Bit_AU u_4_bit_au_4 (
    .in_1(in_1[3:0]), .in_2(in_2), .in_3(in_4), .in_5(in_5[3:0]), .out_7(n4_bit_au_4_out_7), .in_4(in_3),
    .out_6(out_6[3:0]));
endmodule

module _1_Bit_LU (
  input  in_1,
  input  in_2,
  input  [2:0] in_3,
  input  in_4,
  output out_5
);

  wire and_1_out, not_1_out, not_2_out, not_3_out, not_4_out, or_1_out, xor_1_out;

  and and_1 (and_1_out, in_1, in_2);
  not not_1 (not_1_out, or_1_out);
  or or_1 (or_1_out, in_1, in_2);
  xor xor_1 (xor_1_out, in_1, in_2);
  not not_2 (not_2_out, in_1);
  not not_3 (not_3_out, and_1_out);
  not not_4 (not_4_out, xor_1_out);
  Multiplexer #(.select(3)) multiplexer_1 (
    .in0(and_1_out), .in1(not_3_out), .in2(not_1_out), .in3(not_4_out), .in4(or_1_out), .in5(xor_1_out),
    .in6(not_2_out), .in7(not_2_out), .out(out_5), .sel(in_3), .en(in_4));
endmodule

module _4_Bit_LU (
  input  [3:0] in_1,
  input  in_2,
  input  [2:0] in_3,
  input  [3:0] in_4,
  output [3:0] out_5
);

  _1_Bit_LU u_1_bit_lu_1 (.in_1(in_1[3]), .in_2(in_4[3]), .out_5(out_5[3]), .in_3(in_3), .in_4(in_2));
  _1_Bit_LU u_1_bit_lu_2 (.in_1(in_1[2]), .in_2(in_4[2]), .out_5(out_5[2]), .in_3(in_3), .in_4(in_2));
  _1_Bit_LU u_1_bit_lu_3 (.in_1(in_1[1]), .in_2(in_4[1]), .out_5(out_5[1]), .in_3(in_3), .in_4(in_2));
  _1_Bit_LU u_1_bit_lu_4 (.in_1(in_1[0]), .in_2(in_4[0]), .out_5(out_5[0]), .in_3(in_3), .in_4(in_2));
endmodule

module _16_Bit_LU (
  input  [15:0] in_1,
  input  in_2,
  input  [2:0] in_3,
  input  [15:0] in_4,
  output [15:0] out_5
);

  _4_Bit_LU u_4_bit_lu_1 (.in_1(in_1[15:12]), .in_2(in_2), .in_4(in_4[15:12]), .in_3(in_3), .out_5(out_5[15:12]));
  _4_Bit_LU u_4_bit_lu_2 (.in_1(in_1[11:8]), .in_2(in_2), .in_4(in_4[11:8]), .in_3(in_3), .out_5(out_5[11:8]));
  _4_Bit_LU u_4_bit_lu_3 (.in_1(in_1[7:4]), .in_2(in_2), .in_4(in_4[7:4]), .in_3(in_3), .out_5(out_5[7:4]));
  _4_Bit_LU u_4_bit_lu_4 (.in_1(in_1[3:0]), .in_2(in_2), .in_4(in_4[3:0]), .in_3(in_3), .out_5(out_5[3:0]));
endmodule

module _16_Bit_ALU (
  input  [15:0] in_1,
  input  [15:0] in_2,
  input  [4:0] in_3,
  input  in_4,
  output [15:0] out_5,
  output out_6
);

  wire [15:0] n16_bit_au_1_out_6, n16_bit_lu_1_out_5;

  _16_Bit_AU u_16_bit_au_1 (
    .in_1(in_1), .in_4(in_3[0]), .in_2(in_4), .in_5(in_2), .out_7(out_6), .in_3(in_3[2:1]),
    .out_6(n16_bit_au_1_out_6));
  _16_Bit_LU u_16_bit_lu_1 (.in_1(in_1), .in_2(in_4), .in_4(in_2), .in_3(in_3[2:0]), .out_5(n16_bit_lu_1_out_5));
  Multiplexer #(.select(2), .width(16)) multiplexer_1 (
    .in1(n16_bit_lu_1_out_5), .in2(n16_bit_au_1_out_6), .out(out_5), .sel(in_3[4:3]), .en(in_4));  // open: in0, in3
endmodule

module _4_Bit_SU (
  input  in_1,
  input  [3:0] in_2,
  input  in_3,
  input  in_4,
  input  in_5,
  output out_6,
  output [3:0] out_7,
  output out_8
);

  Multiplexer multiplexer_1 (.in0(in_2[3]), .out(out_6), .sel(in_4), .en(in_5));  // open: in1
  Multiplexer multiplexer_2 (.in0(in_2[2]), .in1(in_1), .out(out_7[3]), .sel(in_4), .en(in_5));
  Multiplexer multiplexer_3 (.in0(in_2[1]), .in1(in_2[3]), .out(out_7[2]), .sel(in_4), .en(in_5));
  Multiplexer multiplexer_4 (.in0(in_2[0]), .in1(in_2[2]), .out(out_7[1]), .sel(in_4), .en(in_5));
  Multiplexer multiplexer_5 (.in0(in_3), .in1(in_2[1]), .out(out_7[0]), .sel(in_4), .en(in_5));
  Multiplexer multiplexer_6 (.in1(in_2[0]), .out(out_8), .sel(in_4), .en(in_5));  // open: in0
endmodule

module _16_Bit_SU (
  input  in_1,
  input  in_2,
  input  [15:0] in_3,
  input  in_4,
  input  in_5,
  output out_6,
  output [15:0] out_7,
  output out_8
);

  wire n4_bit_su_1_out_8, n4_bit_su_2_out_6, n4_bit_su_2_out_8, n4_bit_su_3_out_6, n4_bit_su_3_out_8,
       n4_bit_su_4_out_6;

  _4_Bit_SU u_4_bit_su_1 (
    .in_1(in_2), .out_6(out_6), .out_7(out_7[15:12]), .out_8(n4_bit_su_1_out_8), .in_2(in_3[15:12]),
    .in_5(in_1), .in_3(n4_bit_su_2_out_6), .in_4(in_5));
  _4_Bit_SU u_4_bit_su_2 (
    .in_1(n4_bit_su_1_out_8), .out_6(n4_bit_su_2_out_6), .out_7(out_7[11:8]), .out_8(n4_bit_su_2_out_8),
    .in_2(in_3[11:8]), .in_5(in_1), .in_3(n4_bit_su_3_out_6), .in_4(in_5));
  _4_Bit_SU u_4_bit_su_3 (
    .in_1(n4_bit_su_2_out_8), .out_6(n4_bit_su_3_out_6), .out_7(out_7[7:4]), .out_8(n4_bit_su_3_out_8),
    .in_2(in_3[7:4]), .in_5(in_1), .in_3(n4_bit_su_4_out_6), .in_4(in_5));
  _4_Bit_SU u_4_bit_su_4 (
    .in_1(n4_bit_su_3_out_8), .out_6(n4_bit_su_4_out_6), .out_7(out_7[3:0]), .out_8(out_8), .in_2(in_3[3:0]),
    .in_5(in_1), .in_3(in_4), .in_4(in_5));
endmodule

module ControlUnit (
  input  Enable,
  input  [15:0] in_2,
  input  in_3,
  output [1:0] out_4,
  output [2:0] out_5,
  output out_6,
  output [3:0] out_7,
  output [3:0] out_8,
  output [3:0] out_9,
  output [1:0] out_10
);

  wire decoder_2_out0, decoder_2_out1, decoder_2_out2, decoder_2_out3, decoder_2_out4, decoder_2_out5,
       decoder_2_out6, decoder_2_out7, decoder_2_out8, decoder_2_out9, decoder_2_out10, decoder_2_out11,
       decoder_2_out12, decoder_2_out13, decoder_2_out14, decoder_2_out15;
  wire [3:0] counter_1_q;
  wire [15:0] decoder_1_out0;

  Counter #(.width(4), .max('hf)) counter_1 (.Q(counter_1_q), .clk(in_3));  // open: load, D, count, carry, clr
  Decoder #(.select(4)) decoder_1 (
    .out0(decoder_1_out0[0]), .out1(decoder_1_out0[1]), .out2(decoder_1_out0[2]), .out3(decoder_1_out0[3]),
    .out4(decoder_1_out0[4]), .out5(decoder_1_out0[5]), .out6(decoder_1_out0[6]), .out7(decoder_1_out0[7]),
    .out8(decoder_1_out0[8]), .out9(decoder_1_out0[9]), .out10(decoder_1_out0[10]),
    .out11(decoder_1_out0[11]), .out12(decoder_1_out0[12]), .out13(decoder_1_out0[13]),
    .out14(decoder_1_out0[14]), .out15(decoder_1_out0[15]), .sel(in_2[13:10]), .en(Enable));
  Decoder #(.select(4)) decoder_2 (
    .out0(decoder_2_out0), .out1(decoder_2_out1), .out2(decoder_2_out2), .out3(decoder_2_out3),
    .out4(decoder_2_out4), .out5(decoder_2_out5), .out6(decoder_2_out6), .out7(decoder_2_out7),
    .out8(decoder_2_out8), .out9(decoder_2_out9), .out10(decoder_2_out10), .out11(decoder_2_out11),
    .out12(decoder_2_out12), .out13(decoder_2_out13), .out14(decoder_2_out14), .out15(decoder_2_out15),
    .sel(counter_1_q), .en(Enable));
  CombinationalControLogic combinationalcontrologic_1 (
    .in_8(decoder_1_out0), .in_5(in_2[9:0]), .Enable(Enable), .ABUS(out_4), .in_4(decoder_2_out2),
    .in_2(decoder_2_out0), .in_3(decoder_2_out1), .in_6(decoder_2_out3), .in_9(decoder_2_out5),
    .in_7(decoder_2_out4), .in_10(decoder_2_out6), .in_11(decoder_2_out7), .in_12(decoder_2_out8),
    .in_14(decoder_2_out9), .in_15(decoder_2_out10), .in_16(decoder_2_out11), .in_17(decoder_2_out12),
    .in_18(decoder_2_out13), .in_19(decoder_2_out14), .in_20(decoder_2_out15), .AR(out_7), .IR(out_8),
    .PC(out_9), .DBUS(out_5), .Memory(out_10), .S_MUX(out_6));  // open: in_13, in_21
endmodule

module CombinationalControLogic (
  input  Enable,
  input  in_2,
  input  in_3,
  input  in_4,
  input  [9:0] in_5,
  input  in_6,
  input  in_7,
  input  [15:0] in_8,
  input  in_9,
  input  in_10,
  input  in_11,
  input  in_12,
  input  [1:0] in_13,
  input  in_14,
  input  in_15,
  input  in_16,
  input  in_17,
  input  in_18,
  input  in_19,
  input  in_20,
  input  in_21,
  output S_MUX,
  output [3:0] AR,
  output [3:0] IR,
  output [1:0] ABUS,
  output [3:0] PC,
  output [2:0] DBUS,
  output [1:0] Memory
);

  wire and_1_out, and_2_out, and_3_out, and_4_out, and_5_out, and_8_out, and_9_out, and_10_out, and_11_out,
       and_12_out, and_13_out, not_1_out, not_2_out, not_3_out, not_4_out, not_5_out, not_6_out, not_7_out,
       not_8_out, not_9_out, not_10_out, not_11_out, not_12_out, not_13_out, not_14_out, not_15_out,
       not_16_out, not_17_out, not_18_out, not_19_out, not_20_out, not_21_out, not_22_out, not_23_out;
  wire [0:0] and_7_out;
  wire [1:0] or_2_out;
  wire [7:0] or_1_out;

  not not_1 (not_1_out, 1'b0);
  not not_2 (not_2_out, 1'b0);
  not not_3 (not_3_out, in_8[0]);
  not not_4 (not_4_out, in_13[0]);
  not not_5 (not_5_out, 1'b0);
  not not_6 (not_6_out, in_8[0]);
  not not_7 (not_7_out, in_13[1]);
  not not_8 (not_8_out, in_8[0]);
  not not_9 (not_9_out, in_13[1]);
  not not_10 (not_10_out, in_8[0]);
  not not_11 (not_11_out, in_13[0]);
  and and_1 (and_1_out, not_1_out, in_3);
  and and_2 (and_2_out, not_2_out, in_6, not_3_out, in_13[1], not_4_out);
  and and_3 (and_3_out, not_5_out, in_6, not_6_out, not_7_out, in_13[0]);
  not not_12 (not_12_out, 1'b0);
  and and_4 (and_4_out, not_12_out, in_4);
  not not_13 (not_13_out, 1'b0);
  and and_5 (and_5_out, not_13_out, in_6, not_8_out, not_9_out, in_13[0]);
  not not_14 (not_14_out, 1'b0);
  and and_6 (or_2_out[1], not_14_out, in_6, not_10_out, in_13[1], not_11_out);
  not not_15 (not_15_out, 1'b0);
  or or_1 (or_1_out[0], and_1_out, and_2_out, and_3_out);
  or or_2 (or_2_out[0], and_4_out, and_5_out);
  and and_7 (and_7_out[0], not_15_out, in_2);
  _2_1_Encoder u_2_1_encoder_1 (.in_1(or_2_out), .out_2(S_MUX));
  _4_2_Encoder u_4_2_encoder_1 (.in_1({{3{in_21}}, and_7_out[0]}), .out_2(ABUS[0]), .out_3(ABUS[1]));
  _8_3_Encoder u_8_3_encoder_1 (.in_1(or_1_out), .out_2(DBUS[0]), .out_3(DBUS[1]), .out_4(DBUS[2]));
  not not_16 (not_16_out, in_8[0]);
  not not_17 (not_17_out, in_13[1]);
  not not_18 (not_18_out, 1'b0);
  not not_19 (not_19_out, 1'b0);
  not not_20 (not_20_out, 1'b0);
  not not_21 (not_21_out, 1'b0);
  not not_22 (not_22_out, 1'b0);
  not not_23 (not_23_out, 1'b0);
  and and_8 (and_8_out, not_18_out, in_2);
  and and_9 (and_9_out, not_19_out, in_4);
  and and_10 (and_10_out, not_20_out, in_3);
  and and_11 (and_11_out, not_21_out, in_3);
  and and_12 (and_12_out, not_22_out, in_3);
  and and_13 (and_13_out, not_23_out, in_6, not_16_out, not_17_out, in_13[0]);
  or or_3 (AR[3], and_8_out, and_9_out);
  buf or_4 (IR[3], and_10_out);  // OR_Gate
  buf or_5 (PC[2], and_11_out);  // OR_Gate
  or or_6 (Memory[0], and_12_out, and_13_out);

  // Other names for the same wires on the sheet: D0 = in_8[0]; AM0 = in_13[0]; AM1 = in_13[1]; T0 = in_2;
  //   Timing[15:0] = {in_20, in_19, in_18, in_17, in_16, in_15, in_14, in_12, in_11, in_10, in_9, in_7, in_6, in_4, in_3, in_2};
  //   T1 = in_3; T2 = in_4; T3 = in_6; T4 = in_7; T5 = in_9; T6 = in_10; T7 = in_11; T8 = in_12; T9 = in_14;
  //   T10 = in_15; T11 = in_16; T12 = in_17; T13 = in_18; T14 = in_19; T15 = in_20
endmodule

module _16Encoder (
  input  [15:0] in_1,
  output out_2,
  output out_3,
  output out_4,
  output out_5
);

  or or_1 (out_2, in_1[1], in_1[3], in_1[5], in_1[7], in_1[9], in_1[11], in_1[13], in_1[15]);
  or or_2 (out_3, in_1[2], in_1[3], in_1[6], in_1[7], in_1[10], in_1[11], in_1[14], in_1[15]);
  or or_3 (out_4, in_1[4], in_1[5], in_1[6], in_1[7], in_1[12], in_1[13], in_1[14], in_1[15]);
  or or_4 (out_5, in_1[8], in_1[9], in_1[10], in_1[11], in_1[12], in_1[13], in_1[14], in_1[15]);
endmodule

module _8_3_Encoder (
  input  [7:0] in_1,
  output out_2,
  output out_3,
  output out_4
);

  or or_1 (out_2, in_1[1], in_1[3], in_1[5], in_1[7]);
  or or_2 (out_3, in_1[2], in_1[3], in_1[6], in_1[7]);
  or or_3 (out_4, in_1[4], in_1[5], in_1[6], in_1[7]);
endmodule

module _4_2_Encoder (
  input  [3:0] in_1,
  output out_2,
  output out_3
);

  or or_1 (out_2, in_1[1], in_1[3]);
  or or_2 (out_3, in_1[2], in_1[3]);
endmodule

module _2_1_Encoder (
  input  [1:0] in_1,
  output out_2
);


  assign out_2 = in_1[1];
endmodule

module BasicComputer (
  input  ENABLE,
  input  in_2,
  input  in_3,
  input  [2:0] in_4,
  input  [2:0] in_5,
  input  [2:0] in_6,
  input  [2:0] in_7,
  input  [2:0] in_8,
  input  [7:0] in_9,
  input  [4:0] in_10,
  input  [2:0] in_11,
  output [7:0] out_12
);

  wire CLOCK, n16_bit_alu_1_out_6;
  wire [7:0] bit_extender_3_out, INPR_out_6;
  wire [11:0] AR_out_6, bit_extender_1_out, bit_extender_2_out, bit_extender_7_out, PC_out_6;
  wire [15:0] AC, ACI, AR, DBUS, DR, INPR, IR, M, or_1_out, PC, TR;

  Clock clock_1 (.out(CLOCK));
  Bit_Extender #(.in_width(16), .out_width(12)) bit_extender_1 (.in(DBUS), .out(bit_extender_1_out));
  Bit_Extender #(.in_width(16), .out_width(12)) bit_extender_2 (.in(DBUS), .out(bit_extender_2_out));
  Bit_Extender #(.in_width(16), .out_width(8)) bit_extender_3 (.in(DBUS), .out(bit_extender_3_out));
  _12_Bit_Register u_AR (
    .in_1(CLOCK), .out_6(AR_out_6), .in_2(bit_extender_1_out), .in_3(ENABLE), .in_4(in_5));  // open: out_5
  _12_Bit_Register u_PC (
    .in_1(CLOCK), .out_6(PC_out_6), .in_2(bit_extender_2_out), .in_3(ENABLE), .in_4(in_7));  // open: out_5
  _8_Bit_Register u_INPR (.in_1(CLOCK), .out_6(INPR_out_6), .in_2(in_9), .in_3(ENABLE), .in_4(in_11));  // open: out_5
  _8_Bit_Register OUTR (.in_1(CLOCK), .out_6(out_12), .in_2(bit_extender_3_out), .in_3(ENABLE));  // open: out_5, in_4
  assign AR = {{4{1'b0}}, AR_out_6};  // Bit_Extender bit_extender_4
  assign PC = {{4{1'b0}}, PC_out_6};  // Bit_Extender bit_extender_5
  assign INPR = {{8{1'b0}}, INPR_out_6};  // Bit_Extender bit_extender_6
  _16_Bit_Register u_DR (.out_6(DR), .in_1(CLOCK), .in_2(DBUS), .in_3(ENABLE), .in_4(in_4));  // open: out_5
  _16_Bit_Register u_AC (.out_6(AC), .in_1(CLOCK), .in_2(ACI), .in_3(ENABLE), .in_4(in_8));  // open: out_5
  _16_Bit_Register u_TR (.out_6(TR), .in_1(CLOCK), .in_2(DBUS), .in_3(ENABLE));  // open: out_5, in_4
  _16_Bit_Register u_IR (.out_6(IR), .in_1(CLOCK), .in_2(DBUS), .in_3(ENABLE));  // open: out_5, in_4
  Bit_Extender #(.in_width(16), .out_width(12)) bit_extender_7 (.in(AR), .out(bit_extender_7_out));
  assign or_1_out = AC | INPR;  // OR_Gate or_1, 16 bits wide
  Multiplexer #(.select(3), .width(16)) multiplexer_1 (
    .in1(AR), .in2(PC), .in3(DR), .in4(AC), .in5(IR), .in6(TR), .in7(M), .out(DBUS), .sel(in_6), .en(ENABLE));  // open: in0
  _16_Bit_ALU u_16_bit_alu_1 (
    .in_1(DR), .in_2(or_1_out), .out_5(ACI), .out_6(n16_bit_alu_1_out_6), .in_3(in_10), .in_4(ENABLE));
  RAM #(.addrWidth(12), .dataWidth(16), .bus("separate")) ram_1 (
    .addr(bit_extender_7_out), .din(DBUS), .data(M), .str(in_2), .sel(ENABLE), .clk(CLOCK), .ld(in_3));  // open: clr
endmodule

module BasicComputerCU (
  input  [15:0] in_1,
  input  in_2,
  input  [2:0] in_3
);

  wire decoder_1_out0, decoder_1_out1, decoder_1_out2, decoder_1_out3, decoder_1_out4, decoder_1_out5,
       decoder_1_out6, decoder_1_out7;
  wire [3:0] n4_bit_register_1_out_7;

  _4_Bit_Register u_4_bit_register_1 (
    .out_7(n4_bit_register_1_out_7), .in_4(in_2), .in_3(in_3));  // open: out_6, in_2, in_5, in_1
  Decoder #(.select(3)) decoder_1 (
    .out0(decoder_1_out0), .out1(decoder_1_out1), .out2(decoder_1_out2), .out3(decoder_1_out3),
    .out4(decoder_1_out4), .out5(decoder_1_out5), .out6(decoder_1_out6), .out7(decoder_1_out7),
    .sel(in_1[14:12]), .en(in_2));
endmodule
