// Logisim project BasicComputer1.circ as structural Verilog: 7 circuits, main circuit main
module main (
  input  E,
  input  [15:0] in_2,
  input  [15:0] in_3,
  input  [2:0] in_4,
  input  [7:0] in_5,
  output [7:0] out_6
);

  wire Clock;
  wire [2:0] AR_C;
  wire [7:0] bit_extender_2_out, INPR_out_6;
  wire [11:0] AR, bit_extender_1_out, bit_extender_3_out, PC;
  wire [15:0] AC, ALS, bit_extender_5_out, bit_extender_6_out, DB, DR, IR, M, TR;

  Clock clock_1 (.out(Clock));
  Bit_Extender #(.in_width(16), .out_width(12)) bit_extender_1 (.in(DB), .out(bit_extender_1_out));
  Bit_Extender #(.in_width(16), .out_width(8)) bit_extender_2 (.in(DB), .out(bit_extender_2_out));
  _12_Bit_Register u_AR (.in_1(Clock), .out_6(AR), .in_2(bit_extender_1_out), .in_3(E), .in_4(AR_C));  // open: out_5
  _16_Bit_Register Data (.out_6(DR), .in_1(Clock), .in_2(DB), .in_3(E));  // open: out_5, in_4
  _16_Bit_Register u_TR (.out_6(TR), .in_1(Clock), .in_2(DB), .in_3(E));  // open: out_5, in_4
  _8_Bit_Register OUTR (.in_1(Clock), .out_6(out_6), .in_2(bit_extender_2_out), .in_3(E));  // open: out_5, in_4
  RAM #(.addrWidth(12), .dataWidth(16), .bus("separate")) ram_1 (
    .addr(AR), .din(DB), .data(M), .clk(Clock));  // open: str, sel, ld, clr
  Bit_Extender #(.in_width(16), .out_width(12)) bit_extender_3 (.in(DB), .out(bit_extender_3_out));
  _12_Bit_Register u_PC (.in_1(Clock), .out_6(PC), .in_2(bit_extender_3_out), .in_3(E));  // open: out_5, in_4
  _16_Bit_Register u_IR (.out_6(IR), .in_1(Clock), .in_2(DB), .in_3(E));  // open: out_5, in_4
  _16_Bit_Register u_AC (.out_6(AC), .in_1(Clock), .in_2(ALS), .in_3(E));  // open: out_5, in_4
  _8_Bit_Register INPR (.in_1(Clock), .out_6(INPR_out_6), .in_2(in_5), .in_3(E));  // open: out_5, in_4
  ALU16 alu16_1 (.in_3(E), .in_4(DR), .in_5(AC), .out_6(ALS));  // open: in_1, out_7, in_2
  Bit_Extender bit_extender_4 ();  // open: in, out
  assign bit_extender_5_out = {{4{1'b0}}, AR};  // Bit_Extender bit_extender_5
  assign bit_extender_6_out = {{4{1'b0}}, PC};  // Bit_Extender bit_extender_6
  // _8_Bit_Register 8_bit_register_1: pin names not known
  Multiplexer #(.select(3), .width(16)) multiplexer_1 (
    .in1(bit_extender_5_out), .in2(bit_extender_6_out), .in3(DR), .in4(AC), .in5(IR), .in6(TR), .in7(M),
    .out(DB), .en(E));  // open: in0, sel
  Control_Unit control_unit_1 (.out_5(AR_C));  // open: in_1, in_2, in_3, out_4, out_8, out_6, out_7
  Hex_Digit_Display hex_digit_display_1 ();  // open: value, dp
  Multiplexer #(.width(16)) multiplexer_2 ();  // open: in0, in1, out, sel, en
endmodule

module Combinational_Control_Logic (
  input  [11:0] in_1,
  input  [15:0] in_2,
  input  [7:0] in_3,
  input  in_4,
  output SC,
  output [2:0] AC,
  output [2:0] BUS,
  output [2:0] AR,
  output [2:0] PC,
  output [2:0] IR
);

  wire not_1_out;

  not not_1 (not_1_out, in_4);
  and and_1 (SC, in_3[7], not_1_out, in_2[3]);
  // OR_Gate or_1 has open pins: out=AC[0]
  // OR_Gate or_2 has open pins: out=AC[1]
  // OR_Gate or_3 has open pins: out=AC[2]
  buf or_4 (BUS[0], in_2[1]);  // OR_Gate
  or or_5 (BUS[1], in_2[1], in_2[0]);
  buf or_6 (BUS[2], in_2[1]);  // OR_Gate
  buf or_7 (AR[0], 1'b0);  // OR_Gate
  buf or_8 (AR[1], 1'b0);  // OR_Gate
  buf or_9 (AR[2], in_2[0]);  // OR_Gate
  buf or_10 (PC[0], 1'b0);  // OR_Gate
  buf or_11 (PC[1], in_2[1]);  // OR_Gate
  buf or_12 (PC[2], 1'b0);  // OR_Gate
  buf or_13 (IR[0], 1'b0);  // OR_Gate
  buf or_14 (IR[1], 1'b0);  // OR_Gate
  buf or_15 (IR[2], in_2[1]);  // OR_Gate
endmodule

module Control_Unit (
  input  [15:0] in_1,
  input  in_2,
  input  in_3,
  output [2:0] out_4,
  output [2:0] out_5,
  output [2:0] out_6,
  output [2:0] out_7,
  output [3:0] out_8
);

  wire combinational_control_logic_1_sc, d_ff_1_q;
  wire [7:0] decoder_1_out0;
  wire [15:0] decoder_2_out0;

  Counter #(.width(4), .max('hf)) counter_1 (.Q(out_8), .clk(in_3), .clr(d_ff_1_q));  // open: load, D, count, carry
  D_Flip_Flop d_ff_1 (
    .clk(in_3), .D(combinational_control_logic_1_sc), .Q(d_ff_1_q), .en(in_2));  // open: Qn, preset, reset
  Decoder #(.select(3)) decoder_1 (
    .out0(decoder_1_out0[0]), .out1(decoder_1_out0[1]), .out2(decoder_1_out0[2]), .out3(decoder_1_out0[3]),
    .out4(decoder_1_out0[4]), .out5(decoder_1_out0[5]), .out6(decoder_1_out0[6]), .out7(decoder_1_out0[7]),
    .sel(in_1[14:12]), .en(in_2));
  Decoder #(.select(4)) decoder_2 (
    .out0(decoder_2_out0[0]), .out1(decoder_2_out0[1]), .out2(decoder_2_out0[2]), .out3(decoder_2_out0[3]),
    .out4(decoder_2_out0[4]), .out5(decoder_2_out0[5]), .out6(decoder_2_out0[6]), .out7(decoder_2_out0[7]),
    .out8(decoder_2_out0[8]), .out9(decoder_2_out0[9]), .out10(decoder_2_out0[10]),
    .out11(decoder_2_out0[11]), .out12(decoder_2_out0[12]), .out13(decoder_2_out0[13]),
    .out14(decoder_2_out0[14]), .out15(decoder_2_out0[15]), .sel(out_8), .en(in_2));
  Combinational_Control_Logic combinational_control_logic_1 (
    .in_1(in_1[11:0]), .in_3(decoder_1_out0), .in_4(in_1[15]), .in_2(decoder_2_out0),
    .SC(combinational_control_logic_1_sc), .BUS(out_4), .AR(out_5), .PC(out_6), .IR(out_7));  // open: AC
endmodule

module AU16B (
  input  in_1,
  input  [15:0] in_2,
  input  [15:0] in_3,
  input  [1:0] in_4,
  input  in_5,
  output [15:0] out_6,
  output out_7
);

  wire [15:0] multiplexer_1_out, not_1_out;

  assign not_1_out = ~in_3;  // NOT_Gate not_1, 16 bits wide
  Multiplexer #(.select(2), .width(16)) multiplexer_1 (
    .in0(in_3), .in1(not_1_out), .in2({16{1'b0}}), .in3(16'h1), .out(multiplexer_1_out), .sel(in_4), .en(in_5));
  Adder #(.width(16)) adder_1 (.a(in_2), .b(multiplexer_1_out), .out(out_6), .cin(in_1), .cout(out_7));
endmodule

module LU16B (
  input  [15:0] in_1,
  input  [15:0] in_2,
  input  [1:0] in_3,
  input  in_4,
  output [15:0] out_5
);

  wire [15:0] and_1_out, not_1_out, or_1_out, xor_1_out;

  assign and_1_out = in_1 & in_2;  // AND_Gate and_1, 16 bits wide
  assign or_1_out = in_1 | in_2;  // OR_Gate or_1, 16 bits wide
  assign xor_1_out = in_1 ^ in_2;  // XOR_Gate xor_1, 16 bits wide
  assign not_1_out = ~in_1;  // NOT_Gate not_1, 16 bits wide
  Multiplexer #(.select(2), .width(16)) multiplexer_1 (
    .in0(and_1_out), .in1(or_1_out), .in2(xor_1_out), .in3(not_1_out), .out(out_5), .sel(in_3), .en(in_4));
endmodule

module ALU16 (
  input  in_1,
  input  [3:0] in_2,
  input  in_3,
  input  [15:0] in_4,
  input  [15:0] in_5,
  output [15:0] out_6,
  output out_7
);

  wire [15:0] au16b_1_out_6, demultiplexer_1_out0, demultiplexer_1_out1, lu16b_1_out_5, n16su_1_out_6;

  AU16B au16b_1 (
    .in_1(in_1), .in_2(in_4), .in_3(in_5), .in_4(in_2[1:0]), .in_5(in_3), .out_6(au16b_1_out_6), .out_7(out_7));
  LU16B lu16b_1 (.in_1(in_4), .in_2(in_5), .in_3(in_2[1:0]), .in_4(in_3), .out_5(lu16b_1_out_5));
  Demultiplexer #(.width(16)) demultiplexer_1 (
    .out0(demultiplexer_1_out0), .out1(demultiplexer_1_out1), .in(n16su_1_out_6), .sel(in_2[2]), .en(in_3));
  _16SU u_16su_1 (
    .in_1(in_4), .out_6(n16su_1_out_6), .in_2(in_3), .in_5(in_2[2]), .in_4(1'b0), .in_3(1'b0));  // open: out_7, out_8
  Multiplexer #(.select(2), .width(16)) multiplexer_1 (
    .in0(au16b_1_out_6), .in1(lu16b_1_out_5), .in2(demultiplexer_1_out0), .in3(demultiplexer_1_out1),
    .out(out_6), .sel(in_2[3:2]), .en(in_3));
endmodule

module _16SU (
  input  [15:0] in_1,
  input  in_2,
  input  in_3,
  input  in_4,
  input  in_5,
  output [15:0] out_6,
  output out_7,
  output out_8
);

  wire n4_bit_su_1_out_8, n4_bit_su_2_out_6, n4_bit_su_2_out_8, n4_bit_su_3_out_6, n4_bit_su_3_out_8,
       n4_bit_su_4_out_6;

  _4_Bit_SU u_4_bit_su_1 (
    .in_1(in_4), .out_6(out_7), .out_7(out_6[15:12]), .out_8(n4_bit_su_1_out_8), .in_2(in_1[15:12]),
    .in_5(in_2), .in_3(n4_bit_su_2_out_6), .in_4(in_5));
  _4_Bit_SU u_4_bit_su_2 (
    .in_1(n4_bit_su_1_out_8), .out_6(n4_bit_su_2_out_6), .out_7(out_6[11:8]), .out_8(n4_bit_su_2_out_8),
    .in_2(in_1[11:8]), .in_5(in_2), .in_3(n4_bit_su_3_out_6), .in_4(in_5));
  _4_Bit_SU u_4_bit_su_3 (
    .in_1(n4_bit_su_2_out_8), .out_6(n4_bit_su_3_out_6), .out_7(out_6[7:4]), .out_8(n4_bit_su_3_out_8),
    .in_2(in_1[7:4]), .in_5(in_2), .in_3(n4_bit_su_4_out_6), .in_4(in_5));
  _4_Bit_SU u_4_bit_su_4 (
    .in_1(n4_bit_su_3_out_8), .out_6(n4_bit_su_4_out_6), .out_7(out_6[3:0]), .out_8(out_8), .in_2(in_1[3:0]),
    .in_5(in_2), .in_3(in_3), .in_4(in_5));
endmodule
