// Logisim project Components.circ as structural Verilog: 27 circuits, main circuit main
module main (
  input  in_1,
  input  [2:0] in_2,
  input  [1:0] in_3,
  input  [1:0] in_4,
  input  [2:0] in_5,
  input  [2:0] in_6,
  input  [2:0] in_7
);

  wire clock_1_out;
  wire [7:0] demultiplexer_1_out0, demultiplexer_1_out1, demultiplexer_1_out2, demultiplexer_1_out3,
       multiplexer_1_out, n8_bit_register_1_out_6, n8_bit_register_2_out_6, n8_bit_register_3_out_6,
       n8_bit_register_4_out_6;

  Clock clock_1 (.out(clock_1_out));
  _8_Bit_Register u_8_bit_register_1 (
    .in_1(clock_1_out), .out_6(n8_bit_register_1_out_6), .in_2(demultiplexer_1_out0), .in_3(in_1), .in_4(in_2));  // open: out_5
  _8_Bit_Register u_8_bit_register_2 (
    .in_1(clock_1_out), .out_6(n8_bit_register_2_out_6), .in_2(demultiplexer_1_out1), .in_3(in_1), .in_4(in_5));  // open: out_5
  _8_Bit_Register u_8_bit_register_3 (
    .in_1(clock_1_out), .out_6(n8_bit_register_3_out_6), .in_2(demultiplexer_1_out2), .in_3(in_1), .in_4(in_6));  // open: out_5
  _8_Bit_Register u_8_bit_register_4 (
    .in_1(clock_1_out), .out_6(n8_bit_register_4_out_6), .in_2(demultiplexer_1_out3), .in_3(in_1), .in_4(in_7));  // open: out_5
  Multiplexer #(.select(2), .width(8)) multiplexer_1 (
    .in0(n8_bit_register_1_out_6), .in1(n8_bit_register_2_out_6), .in2(n8_bit_register_3_out_6),
    .in3(n8_bit_register_4_out_6), .out(multiplexer_1_out), .sel(in_3), .en(in_1));
  Demultiplexer #(.select(2), .width(8)) demultiplexer_1 (
    .out0(demultiplexer_1_out0), .out1(demultiplexer_1_out1), .out2(demultiplexer_1_out2),
    .out3(demultiplexer_1_out3), .in(multiplexer_1_out), .sel(in_4), .en(in_1));
endmodule

module _1_Bit_Register (
  input  in_1,
  input  in_2,
  input  in_3,
  input  in_4,
  input  [2:0] in_5,
  output out_6,
  output out_7
);

  wire and_2_out, and_3_out, multiplexer_1_out, not_1_out, not_2_out, not_3_out, xor_1_out;
  wire [1:0] or_1_out;

  xor xor_1 (xor_1_out, in_3, out_6);
  not not_1 (not_1_out, in_5[0]);
  not not_2 (not_2_out, in_5[1]);
  and and_1 (or_1_out[1], not_2_out, not_3_out);
  not not_3 (not_3_out, in_5[2]);
  and and_2 (and_2_out, not_1_out, not_3_out);
  and and_3 (and_3_out, not_3_out, in_5[1]);
  Multiplexer #(.select(2)) multiplexer_1 (
    .in0(in_2), .in1(xor_1_out), .in2(1'b0), .in3(out_6), .out(multiplexer_1_out), .sel(or_1_out), .en(in_4));
  or or_1 (or_1_out[0], and_2_out, and_3_out);
  D_FF d_ff_1 (.in_2(multiplexer_1_out), .out_4(out_6), .in_1(in_1), .in_3(in_4));  // open: out_5
  and and_4 (out_7, out_6, in_3);
endmodule

module _4_Bit_Register (
  input  in_1,
  input  [3:0] in_2,
  input  [2:0] in_3,
  input  in_4,
  input  in_5,
  output out_6,
  output [3:0] out_7
);

  wire n1_bit_register_2_out_7, n1_bit_register_3_out_7, n1_bit_register_4_out_7;

  _1_Bit_Register u_1_bit_register_1 (
    .in_2(in_2[3]), .in_3(n1_bit_register_2_out_7), .out_6(out_7[3]), .in_4(in_4), .out_7(out_6),
    .in_5(in_3), .in_1(in_1));
  _1_Bit_Register u_1_bit_register_2 (
    .in_2(in_2[2]), .in_3(n1_bit_register_3_out_7), .out_6(out_7[2]), .in_4(in_4),
    .out_7(n1_bit_register_2_out_7), .in_5(in_3), .in_1(in_1));
  _1_Bit_Register u_1_bit_register_3 (
    .in_2(in_2[1]), .in_3(n1_bit_register_4_out_7), .out_6(out_7[1]), .in_4(in_4),
    .out_7(n1_bit_register_3_out_7), .in_5(in_3), .in_1(in_1));
  _1_Bit_Register u_1_bit_register_4 (
    .in_2(in_2[0]), .in_3(in_5), .out_6(out_7[0]), .in_4(in_4), .out_7(n1_bit_register_4_out_7), .in_5(in_3),
    .in_1(in_1));
endmodule

module _5_Bit_Register (
  input  in_1,
  input  [4:0] in_2,
  input  in_3,
  input  [2:0] in_4,
  output out_5,
  output [4:0] out_6
);

  wire n4_bit_register_1_out_6;

  _1_Bit_Register u_1_bit_register_1 (
    .in_2(in_2[4]), .in_3(n4_bit_register_1_out_6), .out_6(out_6[4]), .in_4(in_3), .out_7(out_5),
    .in_5(in_4), .in_1(in_1));
  _4_Bit_Register u_4_bit_register_1 (
    .out_6(n4_bit_register_1_out_6), .out_7(out_6[3:0]), .in_2(in_2[3:0]), .in_4(in_3), .in_3(in_4),
    .in_5(1'b1), .in_1(in_1));
endmodule

module _8_Bit_Register (
  input  in_1,
  input  [7:0] in_2,
  input  in_3,
  input  [2:0] in_4,
  output out_5,
  output [7:0] out_6
);

  wire n4_bit_register_2_out_6;

  _4_Bit_Register u_4_bit_register_1 (
    .out_6(out_5), .out_7(out_6[7:4]), .in_2(in_2[7:4]), .in_4(in_3), .in_3(in_4),
    .in_5(n4_bit_register_2_out_6), .in_1(in_1));
  _4_Bit_Register u_4_bit_register_2 (
    .out_6(n4_bit_register_2_out_6), .out_7(out_6[3:0]), .in_2(in_2[3:0]), .in_4(in_3), .in_3(in_4),
    .in_5(1'b1), .in_1(in_1));
endmodule

module _10_Bit_Register (
  input  in_1,
  input  [9:0] in_2,
  input  [2:0] in_3,
  input  in_4,
  output out_5,
  output [9:0] out_6
);

  wire n1_bit_register_2_out_7, n4_bit_register_1_out_6, n4_bit_register_2_out_6;

  _1_Bit_Register u_1_bit_register_1 (
    .in_2(in_2[9]), .in_3(n1_bit_register_2_out_7), .out_6(out_6[9]), .in_4(in_4), .out_7(out_5),
    .in_5(in_3), .in_1(in_1));
  _1_Bit_Register u_1_bit_register_2 (
    .in_2(in_2[8]), .in_3(n4_bit_register_1_out_6), .out_6(out_6[8]), .in_4(in_4),
    .out_7(n1_bit_register_2_out_7), .in_5(in_3), .in_1(in_1));
  _4_Bit_Register u_4_bit_register_1 (
    .out_6(n4_bit_register_1_out_6), .out_7(out_6[7:4]), .in_2(in_2[7:4]), .in_4(in_4), .in_3(in_3),
    .in_5(n4_bit_register_2_out_6), .in_1(in_1));
  _4_Bit_Register u_4_bit_register_2 (
    .out_6(n4_bit_register_2_out_6), .out_7(out_6[3:0]), .in_2(in_2[3:0]), .in_4(in_4), .in_3(in_3),
    .in_5(1'b1), .in_1(in_1));
endmodule

module _12_Bit_Register (
  input  in_1,
  input  [11:0] in_2,
  input  in_3,
  input  [2:0] in_4,
  output out_5,
  output [11:0] out_6
);

  wire n4_bit_register_2_out_6, n4_bit_register_3_out_6;

  _4_Bit_Register u_4_bit_register_1 (
    .out_6(out_5), .out_7(out_6[11:8]), .in_2(in_2[11:8]), .in_4(in_3), .in_3(in_4),
    .in_5(n4_bit_register_2_out_6), .in_1(in_1));
  _4_Bit_Register u_4_bit_register_2 (
    .out_6(n4_bit_register_2_out_6), .out_7(out_6[7:4]), .in_2(in_2[7:4]), .in_4(in_3), .in_3(in_4),
    .in_5(n4_bit_register_3_out_6), .in_1(in_1));
  _4_Bit_Register u_4_bit_register_3 (
    .out_6(n4_bit_register_3_out_6), .out_7(out_6[3:0]), .in_2(in_2[3:0]), .in_4(in_3), .in_3(in_4),
    .in_5(1'b1), .in_1(in_1));
endmodule

module _16_Bit_Register (
  input  in_1,
  input  [15:0] in_2,
  input  in_3,
  input  [2:0] in_4,
  output out_5,
  output [15:0] out_6
);

  wire n4_bit_register_2_out_6, n4_bit_register_3_out_6, n4_bit_register_4_out_6;

  _4_Bit_Register u_4_bit_register_1 (
    .out_6(out_5), .out_7(out_6[15:12]), .in_2(in_2[15:12]), .in_4(in_3), .in_3(in_4),
    .in_5(n4_bit_register_2_out_6), .in_1(in_1));
  _4_Bit_Register u_4_bit_register_2 (
    .out_6(n4_bit_register_2_out_6), .out_7(out_6[11:8]), .in_2(in_2[11:8]), .in_4(in_3), .in_3(in_4),
    .in_5(n4_bit_register_3_out_6), .in_1(in_1));
  _4_Bit_Register u_4_bit_register_3 (
    .out_6(n4_bit_register_3_out_6), .out_7(out_6[7:4]), .in_2(in_2[7:4]), .in_4(in_3), .in_3(in_4),
    .in_5(n4_bit_register_4_out_6), .in_1(in_1));
  _4_Bit_Register u_4_bit_register_4 (
    .out_6(n4_bit_register_4_out_6), .out_7(out_6[3:0]), .in_2(in_2[3:0]), .in_4(in_3), .in_3(in_4),
    .in_5(1'b1), .in_1(in_1));
endmodule

module Half_Adder (
  input  X,
  input  Y,
  output S,
  output C
);

  xor xor_1 (S, X, Y);
  and and_1 (C, X, Y);
endmodule

module Full_Adder (
  input  in_1,
  input  in_2,
  input  in_3,
  output out_4,
  output out_5
);

  wire half_adder_1_c, half_adder_1_s, half_adder_2_c;

  Half_Adder half_adder_1 (.X(in_1), .Y(in_2), .S(half_adder_1_s), .C(half_adder_1_c));
  Half_Adder half_adder_2 (.X(half_adder_1_s), .Y(in_3), .S(out_4), .C(half_adder_2_c));
  or or_1 (out_5, half_adder_2_c, half_adder_1_c);
endmodule

module _1_Bit_AU (
  input  in_1,
  input  in_2,
  input  in_3,
  input  [1:0] in_4,
  input  in_5,
  output out_6,
  output out_7
);

  wire multiplexer_1_out, not_1_out, not_2_out;

  not not_1 (not_1_out, in_2);
  not not_2 (not_2_out, 1'b0);
  Multiplexer #(.select(2)) multiplexer_1 (
    .in0(1'b0), .in1(in_2), .in2(not_1_out), .in3(not_2_out), .out(multiplexer_1_out), .sel(in_4), .en(in_3));
  FullAdder fulladder_1 (.in_1(in_1), .in_2(multiplexer_1_out), .in_3(in_5), .out_4(out_6), .out_5(out_7));
endmodule

module _4_Bit_AU (
  input  [3:0] in_1,
  input  in_2,
  input  in_3,
  input  [1:0] in_4,
  input  [3:0] in_5,
  output [3:0] out_6,
  output out_7
);

  wire n1_bit_au_2_out_7, n1_bit_au_3_out_7, n1_bit_au_4_out_7;

  _1_Bit_AU u_1_bit_au_1 (
    .in_1(in_1[3]), .in_2(in_5[3]), .out_6(out_6[3]), .out_7(out_7), .in_3(in_2), .in_4(in_4),
    .in_5(n1_bit_au_2_out_7));
  _1_Bit_AU u_1_bit_au_2 (
    .in_1(in_1[2]), .in_2(in_5[2]), .out_6(out_6[2]), .out_7(n1_bit_au_2_out_7), .in_3(in_2), .in_4(in_4),
    .in_5(n1_bit_au_3_out_7));
  _1_Bit_AU u_1_bit_au_3 (
    .in_1(in_1[1]), .in_2(in_5[1]), .out_6(out_6[1]), .out_7(n1_bit_au_3_out_7), .in_3(in_2), .in_4(in_4),
    .in_5(n1_bit_au_4_out_7));
  _1_Bit_AU u_1_bit_au_4 (
    .in_1(in_1[0]), .in_2(in_5[0]), .out_6(out_6[0]), .out_7(n1_bit_au_4_out_7), .in_3(in_2), .in_4(in_4),
    .in_5(in_3));
endmodule

module _16_Bit_AU (
  input  [15:0] in_1,
  input  in_2,
  input  [1:0] in_3,
  input  in_4,
  input  [15:0] in_5,
  output [15:0] out_6,
  output out_7
);

  wire n4_bit_au_2_out_7, n4_bit_au_3_out_7, n4_bit_au_4_out_7;

  _4_Bit_AU u_4_bit_au_1 (
    .in_1(in_1[15:12]), .in_2(in_2), .in_3(n4_bit_au_2_out_7), .in_5(in_5[15:12]), .out_7(out_7),
    .in_4(in_3), .out_6(out_6[15:12]));
  _4_Bit_AU u_4_bit_au_2 (
    .in_1(in_1[11:8]), .in_2(in_2), .in_3(n4_bit_au_3_out_7), .in_5(in_5[11:8]), .out_7(n4_bit_au_2_out_7),
    .in_4(in_3), .out_6(out_6[11:8]));
  _4_Bit_AU u_4_bit_au_3 (
    .in_1(in_1[7:4]), .in_2(in_2), .in_3(n4_bit_au_4_out_7), .in_5(in_5[7:4]), .out_7(n4_bit_au_3_out_7),
    .in_4(in_3), .out_6(out_6[7:4]));
  _4_Bit_AU u_4_bit_au_4 (
    .in_1(in_1[3:0]), .in_2(in_2), .in_3(in_4), .in_5(in_5[3:0]), .out_7(n4_bit_au_4_out_7), .in_4(in_3),
    .out_6(out_6[3:0]));
endmodule

module _1_Bit_LU (
  input  in_1,
  input  in_2,
  input  [2:0] in_3,
  input  in_4,
  output out_5
);

  wire and_1_out, not_1_out, not_2_out, not_3_out, not_4_out, or_1_out, xor_1_out;

  and and_1 (and_1_out, in_1, in_2);
  not not_1 (not_1_out, or_1_out);
  or or_1 (or_1_out, in_1, in_2);
  xor xor_1 (xor_1_out, in_1, in_2);
  not not_2 (not_2_out, in_1);
  not not_3 (not_3_out, and_1_out);
  not not_4 (not_4_out, xor_1_out);
  Multiplexer #(.select(3)) multiplexer_1 (
    .in0(and_1_out), .in1(not_3_out), .in2(not_1_out), .in3(not_4_out), .in4(or_1_out), .in5(xor_1_out),
    .in6(not_2_out), .in7(not_2_out), .out(out_5), .sel(in_3), .en(in_4));
endmodule

module _4_Bit_LU (
  input  [3:0] in_1,
  input  in_2,
  input  [2:0] in_3,
  input  [3:0] in_4,
  output [3:0] out_5
);

  _1_Bit_LU u_1_bit_lu_1 (.in_1(in_1[3]), .in_2(in_4[3]), .out_5(out_5[3]), .in_3(in_3), .in_4(in_2));
  _1_Bit_LU u_1_bit_lu_2 (.in_1(in_1[2]), .in_2(in_4[2]), .out_5(out_5[2]), .in_3(in_3), .in_4(in_2));
  _1_Bit_LU u_1_bit_lu_3 (.in_1(in_1[1]), .in_2(in_4[1]), .out_5(out_5[1]), .in_3(in_3), .in_4(in_2));
  _1_Bit_LU u_1_bit_lu_4 (.in_1(in_1[0]), .in_2(in_4[0]), .out_5(out_5[0]), .in_3(in_3), .in_4(in_2));
endmodule

module _16_Bit_LU (
  input  [15:0] in_1,
  input  in_2,
  input  [2:0] in_3,
  input  [15:0] in_4,
  output [15:0] out_5
);

  _4_Bit_LU u_4_bit_lu_1 (.in_1(in_1[15:12]), .in_2(in_2), .in_4(in_4[15:12]), .in_3(in_3), .out_5(out_5[15:12]));
  _4_Bit_LU u_4_bit_lu_2 (.in_1(in_1[11:8]), .in_2(in_2), .in_4(in_4[11:8]), .in_3(in_3), .out_5(out_5[11:8]));
  _4_Bit_LU u_4_bit_lu_3 (.in_1(in_1[7:4]), .in_2(in_2), .in_4(in_4[7:4]), .in_3(in_3), .out_5(out_5[7:4]));
  _4_Bit_LU u_4_bit_lu_4 (.in_1(in_1[3:0]), .in_2(in_2), .in_4(in_4[3:0]), .in_3(in_3), .out_5(out_5[3:0]));
endmodule

module _4_Bit_SU (
  input  in_1,
  input  [3:0] in_2,
  input  in_3,
  input  in_4,
  input  in_5,
  output out_6,
  output [3:0] out_7,
  output out_8
);

  wire not_1_out;

  not not_1 (not_1_out, in_4);
  Multiplexer multiplexer_1 (.in0(in_2[3]), .out(out_6), .sel(not_1_out), .en(in_5));  // open: in1
  Multiplexer multiplexer_2 (.in0(in_2[2]), .in1(in_1), .out(out_7[3]), .sel(not_1_out), .en(in_5));
  Multiplexer multiplexer_3 (.in0(in_2[1]), .in1(in_2[3]), .out(out_7[2]), .sel(not_1_out), .en(in_5));
  Multiplexer multiplexer_4 (.in0(in_2[0]), .in1(in_2[2]), .out(out_7[1]), .sel(not_1_out), .en(in_5));
  Multiplexer multiplexer_5 (.in0(in_3), .in1(in_2[1]), .out(out_7[0]), .sel(not_1_out), .en(in_5));
  Multiplexer multiplexer_6 (.in1(in_2[0]), .out(out_8), .sel(not_1_out), .en(in_5));  // open: in0
endmodule

module _16_Bit_SU (
  input  [15:0] in_1,
  input  in_2,
  input  [2:0] in_3,
  output [15:0] out_4,
  output out_5
);

  wire and_1_out, and_2_out, and_3_out, multiplexer_1_out, multiplexer_2_out, n4_bit_su_1_out_6,
       n4_bit_su_1_out_8, n4_bit_su_2_out_6, n4_bit_su_2_out_8, n4_bit_su_3_out_6, n4_bit_su_3_out_8,
       n4_bit_su_4_out_6, n4_bit_su_4_out_8, not_1_out, not_2_out, not_3_out, or_1_out, xor_1_out;

  Multiplexer #(.select(3)) multiplexer_1 (
    .in0(1'b0), .in1(in_1[15]), .in2(n4_bit_su_4_out_8), .out(multiplexer_1_out), .sel(in_3), .en(in_2));  // open: in3, in4, in5, in6, in7
  _4_Bit_SU u_4_bit_su_1 (
    .in_1(multiplexer_1_out), .out_6(n4_bit_su_1_out_6), .out_7(out_4[15:12]), .out_8(n4_bit_su_1_out_8),
    .in_2(in_1[15:12]), .in_5(in_2), .in_3(n4_bit_su_2_out_6), .in_4(or_1_out));
  _4_Bit_SU u_4_bit_su_2 (
    .in_1(n4_bit_su_1_out_8), .out_6(n4_bit_su_2_out_6), .out_7(out_4[11:8]), .out_8(n4_bit_su_2_out_8),
    .in_2(in_1[11:8]), .in_5(in_2), .in_3(n4_bit_su_3_out_6), .in_4(or_1_out));
  and and_1 (and_1_out, in_3[2], not_1_out);
  not not_1 (not_1_out, in_3[0]);
  or or_1 (or_1_out, and_1_out, and_2_out, and_3_out);
  and and_2 (and_2_out, in_3[2], not_2_out);
  and and_3 (and_3_out, not_3_out, in_3[1], in_3[0]);
  not not_2 (not_2_out, in_3[1]);
  not not_3 (not_3_out, in_3[2]);
  xor xor_1 (xor_1_out, in_1[15], in_1[14]);
  _4_Bit_SU u_4_bit_su_3 (
    .in_1(n4_bit_su_2_out_8), .out_6(n4_bit_su_3_out_6), .out_7(out_4[7:4]), .out_8(n4_bit_su_3_out_8),
    .in_2(in_1[7:4]), .in_5(in_2), .in_3(n4_bit_su_4_out_6), .in_4(or_1_out));
  _4_Bit_SU u_4_bit_su_4 (
    .in_1(n4_bit_su_3_out_8), .out_6(n4_bit_su_4_out_6), .out_7(out_4[3:0]), .out_8(n4_bit_su_4_out_8),
    .in_2(in_1[3:0]), .in_5(in_2), .in_3(multiplexer_2_out), .in_4(or_1_out));
  Multiplexer #(.select(3)) multiplexer_2 (
    .in3(1'b0), .in4(1'b0), .in5(n4_bit_su_1_out_6), .in6(1'b0), .out(multiplexer_2_out), .sel(in_3),
    .en(in_2));  // open: in0, in1, in2, in7
  Multiplexer #(.select(3)) multiplexer_3 (
    .in0(1'b0), .in1(1'b0), .in2(1'b0), .in3(1'b0), .in4(xor_1_out), .in5(1'b0), .in6(xor_1_out), .in7(1'b0),
    .out(out_5), .sel(in_3), .en(in_2));
endmodule

module _16_Bit_ALU (
  input  [7:0] in_1,
  input  [15:0] in_2,
  input  [15:0] in_3,
  input  [3:0] in_4,
  input  in_5,
  output [7:0] out_6,
  output [15:0] out_7
);

  wire n16_bit_au_1_out_7;
  wire [15:0] n16_bit_au_1_out_6, n16_bit_lu_1_out_5, n16_bit_su_1_out_4;

  _16_Bit_SU u_16_bit_su_1 (
    .in_1(in_2), .out_4(n16_bit_su_1_out_4), .in_2(in_5), .in_3({in_4[1:0], in_1[0]}), .out_5(out_6[1]));
  _16_Bit_AU u_16_bit_au_1 (
    .in_1(in_2), .in_4(in_1[0]), .in_2(in_5), .in_5(in_3), .out_7(n16_bit_au_1_out_7), .in_3(in_4[1:0]),
    .out_6(n16_bit_au_1_out_6));
  _16_Bit_LU u_16_bit_lu_1 (
    .in_1(in_2), .in_2(in_5), .in_4(in_3), .in_3({in_4[1:0], in_1[0]}), .out_5(n16_bit_lu_1_out_5));
  Multiplexer #(.select(2), .width(16)) multiplexer_1 (
    .in0(n16_bit_su_1_out_4), .in1(n16_bit_lu_1_out_5), .in2(n16_bit_au_1_out_6),
    .out({out_6[2], out_7[14:0]}), .sel(in_4[3:2]), .en(in_5));  // open: in3
  Multiplexer #(.select(2)) multiplexer_2 (
    .in0(1'b0), .in1(1'b0), .in2(n16_bit_au_1_out_7), .in3(1'b0), .out(out_6[0]), .sel(in_4[3:2]), .en(in_5));
  nor nor_1 (out_6[3], out_7[0], out_7[1], out_7[2], out_7[3], out_7[4], out_7[5], out_7[6], out_7[7], out_7[8], out_7[9], out_7[10], out_7[11], out_7[12], out_7[13], out_7[14], out_6[2]);

  assign out_7[15] = out_6[2];
endmodule

module _16Encoder (
  input  [15:0] in_1,
  output out_2,
  output out_3,
  output out_4,
  output out_5
);

  or or_1 (out_2, in_1[1], in_1[3], in_1[5], in_1[7], in_1[9], in_1[11], in_1[13], in_1[15]);
  or or_2 (out_3, in_1[2], in_1[3], in_1[6], in_1[7], in_1[10], in_1[11], in_1[14], in_1[15]);
  or or_3 (out_4, in_1[4], in_1[5], in_1[6], in_1[7], in_1[12], in_1[13], in_1[14], in_1[15]);
  or or_4 (out_5, in_1[8], in_1[9], in_1[10], in_1[11], in_1[12], in_1[13], in_1[14], in_1[15]);
endmodule

module _8_3_Encoder (
  input  [7:0] in_1,
  output out_2,
  output out_3,
  output out_4
);

  or or_1 (out_2, in_1[1], in_1[3], in_1[5], in_1[7]);
  or or_2 (out_3, in_1[2], in_1[3], in_1[6], in_1[7]);
  or or_3 (out_4, in_1[4], in_1[5], in_1[6], in_1[7]);
endmodule

module _4_2_Encoder (
  input  [3:0] in_1,
  output out_2,
  output out_3
);

  or or_1 (out_2, in_1[1], in_1[3]);
  or or_2 (out_3, in_1[2], in_1[3]);
endmodule

module _2_1_Encoder (
  input  [1:0] in_1,
  output out_2
);


  assign out_2 = in_1[1];
endmodule

module SR_FF (
  input  in_1,
  input  in_2,
  input  in_3,
  input  in_4,
  output out_5,
  output out_6
);

  wire and_1_out, and_2_out, or_1_out, or_2_out;

  and and_1 (and_1_out, in_1, in_2, in_3);
  and and_2 (and_2_out, in_3, in_2, in_4);
  or or_1 (or_1_out, and_1_out, out_6);
  or or_2 (or_2_out, out_5, and_2_out);
  not not_1 (out_5, or_1_out);
  not not_2 (out_6, or_2_out);
endmodule

module D_FF (
  input  in_1,
  input  in_2,
  input  in_3,
  output out_4,
  output out_5
);

  wire not_1_out, not_2_out, sr_ff_1_out_5, sr_ff_1_out_6;

  not not_1 (not_1_out, in_2);
  not not_2 (not_2_out, in_1);
  SR_FF sr_ff_1 (
    .in_1(not_1_out), .in_2(not_2_out), .in_3(in_3), .in_4(in_2), .out_5(sr_ff_1_out_5), .out_6(sr_ff_1_out_6));
  SR_FF sr_ff_2 (.in_1(sr_ff_1_out_6), .in_2(in_1), .in_3(in_3), .in_4(sr_ff_1_out_5), .out_5(out_4), .out_6(out_5));
endmodule

module HalfAdder (
  input  in_1,
  input  in_2,
  output out_3,
  output out_4
);

  and and_1 (out_3, in_1, in_2);
  xor xor_1 (out_4, in_1, in_2);
endmodule

module FullAdder (
  input  in_1,
  input  in_2,
  input  in_3,
  output out_4,
  output out_5
);

  wire halfadder_1_out_3, halfadder_1_out_4, halfadder_2_out_3;

  HalfAdder halfadder_1 (.in_1(in_1), .in_2(in_2), .out_3(halfadder_1_out_3), .out_4(halfadder_1_out_4));
  HalfAdder halfadder_2 (.in_1(halfadder_1_out_4), .in_2(in_3), .out_3(halfadder_2_out_3), .out_4(out_4));
  or or_1 (out_5, halfadder_2_out_3, halfadder_1_out_3);
endmodule
