// Logisim project Computer.circ as structural Verilog: 4 circuits, main circuit main
module main (
  input  in_1,
  input  in_2,
  input  [15:0] in_3,
  input  [2:0] in_4,
  input  [2:0] in_5,
  input  in_6,
  input  [7:0] in_7,
  input  [2:0] in_8,
  input  [2:0] in_9,
  input  [2:0] in_10,
  input  in_11,
  input  [3:0] in_12,
  input  [4:0] in_13,
  output [15:0] out_14,
  output [7:0] out_15
);

  wire ARIC, Clock, MLOAD;
  wire [1:0] ABUSC;
  wire [2:0] ARC, controlunit_1_out_5, IRC, PCC, XC;
  wire [3:0] controlunit_1_out_13;
  wire [4:0] X_out_6;
  wire [7:0] bit_extender_2_out, CCRin, CCRout, INPR_out_6;
  wire [9:0] adder_1_out, AR, ARI, bit_extender_3_out, bit_extender_4_out, bit_extender_6_out,
       bit_extender_7_out, bit_extender_8_out, bit_extender_9_out, multiplexer_4_out, PC, SP;
  wire [15:0] ABUS, AC, ACI, ALUBUS, DBUS, GPRA, GPRB, INPR, IR, M, X;

  Clock clock_1 (.out(Clock));
  _16_Bit_Register u_GPRA (.out_6(GPRA), .in_1(Clock), .in_2(DBUS), .in_3(in_1), .in_4(in_4));  // open: out_5
  _10_Bit_Register u_AR (.in_1(Clock), .out_6(AR), .in_2(ARI), .in_4(in_1), .in_3(ARC));  // open: out_5
  assign INPR = {{8{1'b0}}, INPR_out_6};  // Bit_Extender bit_extender_1
  _8_Bit_Register u_INPR (.in_1(Clock), .out_6(INPR_out_6), .in_2(in_7), .in_3(in_1), .in_4(in_8));  // open: out_5
  Bit_Extender #(.in_width(16), .out_width(8)) bit_extender_2 (.in(DBUS), .out(bit_extender_2_out));
  _16_Bit_Register u_GPRB (.out_6(GPRB), .in_1(Clock), .in_2(DBUS), .in_3(in_1));  // open: out_5, in_4
  Bit_Extender #(.in_width(16), .out_width(10)) bit_extender_3 (.in(DBUS), .out(bit_extender_3_out));
  _8_Bit_Register OUTR (
    .in_1(Clock), .out_6(out_15), .in_2(bit_extender_2_out), .in_3(in_1), .in_4(in_9));  // open: out_5
  _10_Bit_Register u_PC (.in_1(Clock), .out_6(PC), .in_2(bit_extender_3_out), .in_4(in_1), .in_3(PCC));  // open: out_5
  _8_Bit_Register CCR (.in_1(Clock), .out_6(CCRout), .in_2(CCRin), .in_3(in_1), .in_4(in_10));  // open: out_5
  _16_Bit_Register u_IR (.out_6(IR), .in_1(Clock), .in_2(DBUS), .in_3(in_1), .in_4(IRC));  // open: out_5
  Bit_Extender #(.in_width(16), .out_width(10)) bit_extender_4 (.in(DBUS), .out(bit_extender_4_out));
  _10_Bit_Register u_SP (.in_1(Clock), .out_6(SP), .in_2(bit_extender_4_out), .in_4(in_1));  // open: out_5, in_3
  _5_Bit_Register u_X (.out_6(X_out_6), .in_2(in_13), .in_4(XC), .in_3(in_1), .in_1(Clock));  // open: out_5
  assign X = {{11{1'b0}}, X_out_6};  // Bit_Extender bit_extender_5
  _16_Bit_Register u_AC (.out_6(AC), .in_1(Clock), .in_2(ACI), .in_3(in_1), .in_4(in_5));  // open: out_5
  ControlUnit controlunit_1 (
    .in_2(IR), .in_3(in_1), .out_5(controlunit_1_out_5), .in_4(Clock), .out_6(ARC),
    .out_13(controlunit_1_out_13), .out_7(ABUSC), .out_8(ARIC), .out_9(XC), .out_10(PCC), .out_11(MLOAD),
    .out_12(IRC), .in_1(CCRout));
  Hex_Digit_Display hex_digit_display_1 (.value(controlunit_1_out_13));  // open: dp
  Multiplexer #(.select(3), .width(16)) multiplexer_1 (
    .in0(M), .in1(ABUS), .in2(GPRB), .in3(AC), .in4(GPRA), .in5(X), .in6(INPR), .in7(IR), .out(DBUS),
    .sel(controlunit_1_out_5), .en(in_1));
  Bit_Extender #(.in_width(16), .out_width(10)) bit_extender_6 (.in(ABUS), .out(bit_extender_6_out));
  Bit_Extender #(.in_width(16), .out_width(10)) bit_extender_7 (.in(IR), .out(bit_extender_7_out));
  Bit_Extender #(.in_width(16), .out_width(10)) bit_extender_8 (.in(X), .out(bit_extender_8_out));
  Adder #(.width(10)) adder_1 (.a(bit_extender_8_out), .b(bit_extender_9_out), .out(adder_1_out));  // open: cin, cout
  Bit_Extender #(.in_width(16), .out_width(10)) bit_extender_9 (.in(DBUS), .out(bit_extender_9_out));
  RAM #(.addrWidth(10), .dataWidth(16), .bus("separate")) ram_1 (
    .addr(bit_extender_6_out), .din(in_3), .data(M), .str(in_6), .clk(Clock), .ld(MLOAD));  // open: sel, clr
  Multiplexer #(.width(10)) multiplexer_2 (
    .in0(bit_extender_7_out), .in1(adder_1_out), .out(ARI), .sel(ARIC), .en(in_1));
  Multiplexer #(.width(16)) multiplexer_3 (.in0(GPRA), .in1(GPRB), .out(ALUBUS), .sel(in_11), .en(in_1));
  Multiplexer #(.select(2), .width(10)) multiplexer_4 (
    .in0(PC), .in1(AR), .in2(SP), .in3(SP), .out(multiplexer_4_out), .sel(ABUSC), .en(in_1));
  _16_Bit_ALU u_16_bit_alu_1 (
    .in_2(AC), .in_3(ALUBUS), .out_7(out_14), .in_4(in_12), .in_5(in_1), .in_1(CCRout), .out_6(CCRin));
  assign ABUS = {{6{1'b0}}, multiplexer_4_out};  // Bit_Extender bit_extender_10

  // Other names for the same wires on the sheet: E = in_1
endmodule

module CombinationalControlLogic (
  input  in_1,
  input  [9:0] Adressess,
  input  [15:0] OpCode,
  input  [1:0] AdressMode,
  input  [15:0] TimingSignal,
  input  [7:0] in_6,
  output [2:0] PC,
  output [2:0] AR,
  output [2:0] DataBus,
  output [1:0] AdressBus,
  output ARI,
  output MLOAD,
  output [2:0] X,
  output SC__0,
  output [2:0] IR
);

  wire and_2_out, and_3_out, indexed, indirect, not_1_out, not_2_out, not_3_out, not_4_out, not_5_out,
       not_6_out, not_7_out, not_8_out, not_9_out, not_10_out, stack;

  not not_1 (not_1_out, TimingSignal[2]);
  not not_2 (not_2_out, TimingSignal[0]);
  not not_3 (not_3_out, TimingSignal[1]);
  and and_1 (MLOAD, TimingSignal[1], not_4_out);
  not not_4 (not_4_out, in_6[5]);
  and and_2 (and_2_out, TimingSignal[1], not_5_out);
  not not_5 (not_5_out, in_6[5]);
  buf or_1 (PC[0], 1'b0);  // OR_Gate
  buf or_2 (PC[1], TimingSignal[1]);  // OR_Gate
  buf or_3 (PC[2], 1'b0);  // OR_Gate
  buf or_4 (AR[0], 1'b0);  // OR_Gate
  buf or_5 (AR[1], 1'b0);  // OR_Gate
  or or_6 (AR[2], TimingSignal[0], TimingSignal[2]);
  buf or_7 (DataBus[0], TimingSignal[0]);  // OR_Gate
  buf or_8 (DataBus[1], 1'b0);  // OR_Gate
  buf or_9 (DataBus[2], 1'b0);  // OR_Gate
  buf or_10 (AdressBus[0], TimingSignal[1]);  // OR_Gate
  buf or_11 (AdressBus[1], and_3_out);  // OR_Gate
  and and_3 (and_3_out, not_2_out, not_3_out);
  or or_12 (ARI, not_1_out, TimingSignal[0]);
  buf or_13 (X[0], TimingSignal[0]);  // OR_Gate
  buf or_14 (X[1], 1'b0);  // OR_Gate
  buf or_15 (X[2], 1'b0);  // OR_Gate
  buf or_16 (IR[0], 1'b0);  // OR_Gate
  buf or_17 (IR[1], 1'b0);  // OR_Gate
  buf or_18 (IR[2], and_2_out);  // OR_Gate
  not not_6 (not_6_out, AdressMode[0]);
  not not_7 (not_7_out, in_6[5]);
  not not_8 (not_8_out, AdressMode[1]);
  not not_9 (not_9_out, in_6[5]);
  not not_10 (not_10_out, in_6[5]);
  and and_4 (indirect, not_6_out, AdressMode[1], TimingSignal[3], not_7_out);
  and and_5 (indexed, AdressMode[0], not_8_out, TimingSignal[3], not_9_out);
  and and_6 (stack, AdressMode[0], AdressMode[1], TimingSignal[3], not_10_out);

  // Other names for the same wires on the sheet: AM0 = AdressMode[0]; AM1 = AdressMode[1]; R = in_6[5];
  //   T0 = TimingSignal[0]; T1 = TimingSignal[1]; T2 = TimingSignal[2]; T3 = TimingSignal[3]
endmodule

module ControlUnit (
  input  [7:0] in_1,
  input  [15:0] in_2,
  input  in_3,
  input  in_4,
  output [2:0] out_5,
  output [2:0] out_6,
  output [1:0] out_7,
  output out_8,
  output [2:0] out_9,
  output [2:0] out_10,
  output out_11,
  output [2:0] out_12,
  output [3:0] out_13
);

  wire combinationalcontrollogic_1_sc__0;
  wire [15:0] decoder_1_out0, decoder_2_out0;

  Counter #(.width(4), .max('hf)) counter_1 (
    .Q(out_13), .clk(in_4), .clr(combinationalcontrollogic_1_sc__0));  // open: load, D, count, carry
  Decoder #(.select(4)) decoder_1 (
    .out0(decoder_1_out0[0]), .out1(decoder_1_out0[1]), .out2(decoder_1_out0[2]), .out3(decoder_1_out0[3]),
    .out4(decoder_1_out0[4]), .out5(decoder_1_out0[5]), .out6(decoder_1_out0[6]), .out7(decoder_1_out0[7]),
    .out8(decoder_1_out0[8]), .out9(decoder_1_out0[9]), .out10(decoder_1_out0[10]),
    .out11(decoder_1_out0[11]), .out12(decoder_1_out0[12]), .out13(decoder_1_out0[13]),
    .out14(decoder_1_out0[14]), .out15(decoder_1_out0[15]), .sel(in_2[13:10]), .en(in_3));
  Decoder #(.select(4)) decoder_2 (
    .out0(decoder_2_out0[0]), .out1(decoder_2_out0[1]), .out2(decoder_2_out0[2]), .out3(decoder_2_out0[3]),
    .out4(decoder_2_out0[4]), .out5(decoder_2_out0[5]), .out6(decoder_2_out0[6]), .out7(decoder_2_out0[7]),
    .out8(decoder_2_out0[8]), .out9(decoder_2_out0[9]), .out10(decoder_2_out0[10]),
    .out11(decoder_2_out0[11]), .out12(decoder_2_out0[12]), .out13(decoder_2_out0[13]),
    .out14(decoder_2_out0[14]), .out15(decoder_2_out0[15]), .sel(out_13), .en(in_3));
  CombinationalControlLogic combinationalcontrollogic_1 (
    .Adressess(in_2[9:0]), .OpCode(decoder_1_out0), .AdressMode(in_2[15:14]), .TimingSignal(decoder_2_out0),
    .DataBus(out_5), .AR(out_6), .SC__0(combinationalcontrollogic_1_sc__0), .AdressBus(out_7), .ARI(out_8),
    .X(out_9), .PC(out_10), .MLOAD(out_11), .IR(out_12), .in_6(in_1));  // open: in_1
endmodule

module DigitalDesign (
  input  in_1,
  input  S,
  output [7:0] out_3
);

  wire and_1_out, and_2_out, and_3_out, C, CE, F, LABC, not_1_out, or_1_out, or_2_out, subtractor_1_bout,
       T0_out_4, T1, T1_out_4, T2, T2_out_4, T3, T3_out_4, undriven_3, undriven_4;
  wire [1:0] undriven, undriven_2, undriven_6, undriven_7;
  wire [7:0] A_out_6, K2_out, RD, undriven_5;

  Clock clock_1 (.out(C));
  _8_Bit_Register D (.in_1(C), .out_6(out_3), .in_2(RD), .in_3(in_1), .in_4({T3, undriven}));  // open: out_5
  _8_Bit_Register A (.in_1(C), .out_6(A_out_6), .in_3(in_1), .in_4({LABC, undriven_2}));  // open: out_5, in_2
  assign K2_out = or_1_out ? A_out_6 : 8'bz;  // Controlled_Buffer K2
  assign RD = and_2_out ? A_out_6 : 8'bz;  // Controlled_Buffer K1
  and and_1 (and_1_out, T2, CE);
  or or_1 (or_1_out, and_1_out, T1);
  and and_2 (and_2_out, T3, F, CE);
  J_K_Flip_Flop j_k_ff_1 (.J(undriven_3), .clk(C), .K(undriven_4), .Q(F), .en(in_1));  // open: Qn, preset, reset
  Subtractor subtractor_1 (.a(K2_out), .b(undriven_5), .bout(subtractor_1_bout));  // open: out, bin
  D_FF Carry (.in_2(subtractor_1_bout), .out_4(CE), .in_1(C), .in_3(in_1));  // open: out_5
  _8_Bit_Register B (.in_1(C), .in_3(in_1), .in_4({LABC, undriven_6}));  // open: out_5, out_6, in_2
  not not_1 (not_1_out, S);
  and and_3 (and_3_out, T0_out_4, not_1_out);
  and and_4 (LABC, T0_out_4, S);
  _8_Bit_Register u_C (.in_1(C), .in_3(in_1), .in_4({LABC, undriven_7}));  // open: out_5, out_6, in_2
  or or_2 (or_2_out, and_3_out, T3_out_4);
  D_FF T0 (.in_2(or_2_out), .out_4(T0_out_4), .in_1(C), .in_3(in_1));  // open: out_5
  D_FF u_T1 (.in_2(LABC), .out_4(T1_out_4), .in_1(C), .in_3(in_1));  // open: out_5
  D_FF u_T2 (.in_2(T1_out_4), .out_4(T2_out_4), .in_1(C), .in_3(in_1));  // open: out_5
  D_FF u_T3 (.in_2(T2_out_4), .out_4(T3_out_4), .in_1(C), .in_3(in_1));  // open: out_5

  // Other names for the same wires on the sheet: E = in_1
endmodule
