// Logisim project HalfAdder.circ as structural Verilog
module Full_Adder (
  input  X,
  input  Y,
  input  Cn_1,
  output S,
  output Cn
);

  wire and_1_out, and_2_out, xor_1_out;

  xor xor_1 (xor_1_out, Y, Cn_1);
  xor xor_2 (S, X, xor_1_out);
  and and_1 (and_1_out, xor_1_out, X);
  and and_2 (and_2_out, Cn_1, Y);
  or or_1 (Cn, and_1_out, and_2_out);
endmodule

module _4X1Multiplexer (
  input  in_1,
  input  in_2,
  input  in_3,
  input  in_4,
  input  [1:0] in_5,
  output out_6
);

  wire and_1_out, and_2_out, and_3_out, and_4_out, not_1_out, not_2_out, not_3_out, not_4_out;

  and and_1 (and_1_out, in_1, not_1_out, not_2_out);
  not not_1 (not_1_out, in_5[0]);
  not not_2 (not_2_out, in_5[1]);
  not not_3 (not_3_out, in_5[0]);
  and and_2 (and_2_out, in_2, not_3_out, in_5[1]);
  and and_3 (and_3_out, in_3, in_5[0], not_4_out);
  not not_4 (not_4_out, in_5[1]);
  and and_4 (and_4_out, in_4, in_5[0], in_5[1]);
  or or_1 (out_6, and_1_out, and_2_out, and_3_out, and_4_out);

  // Notes on the sheet:
  //   4X1 Multiplexer
endmodule

module _8X1_Multiplexer (
  input  in_1,
  input  in_2,
  input  in_3,
  input  in_4,
  input  in_5,
  input  in_6,
  input  in_7,
  input  in_8,
  input  [2:0] in_9,
  output out_10
);

  wire and_1_out, and_2_out, n4x1multiplexer_1_out_6, n4x1multiplexer_2_out_6, not_1_out;

  _4X1Multiplexer u_4x1multiplexer_1 (
    .in_1(in_1), .in_2(in_2), .in_3(in_3), .in_4(in_4), .out_6(n4x1multiplexer_1_out_6), .in_5(in_9[1:0]));
  _4X1Multiplexer u_4x1multiplexer_2 (
    .in_1(in_5), .in_2(in_6), .in_3(in_7), .in_4(in_8), .out_6(n4x1multiplexer_2_out_6), .in_5(in_9[1:0]));
  not not_1 (not_1_out, in_9[2]);
  and and_1 (and_1_out, n4x1multiplexer_1_out_6, not_1_out);
  and and_2 (and_2_out, n4x1multiplexer_2_out_6, in_9[2]);
  or or_1 (out_10, and_1_out, and_2_out);
endmodule

module _8x1_Multiplexer_2Bit (
  input  [1:0] in_1,
  input  [1:0] in_2,
  input  [1:0] in_3,
  input  [1:0] in_4,
  input  [1:0] in_5,
  input  [1:0] in_6,
  input  [1:0] in_7,
  input  [1:0] in_8,
  input  [2:0] in_9,
  output [1:0] out_10
);

  _8X1_Multiplexer u_8x1_multiplexer_1 (
    .in_1(in_1[0]), .in_2(in_2[0]), .in_3(in_3[0]), .in_4(in_4[0]), .in_5(in_5[0]), .in_6(in_6[0]),
    .in_7(in_7[0]), .in_8(in_8[0]), .in_9(in_9), .out_10(out_10[0]));
  _8X1_Multiplexer u_8x1_multiplexer_2 (
    .in_1(in_1[1]), .in_2(in_2[1]), .in_3(in_3[1]), .in_4(in_4[1]), .in_5(in_5[1]), .in_6(in_6[1]),
    .in_7(in_7[1]), .in_8(in_8[1]), .in_9(in_9), .out_10(out_10[1]));
endmodule

module _8X1_Multiplexer_4Bit (
  input  [3:0] in_1,
  input  [3:0] in_2,
  input  [3:0] in_3,
  input  [3:0] in_4,
  input  [3:0] in_5,
  input  [3:0] in_6,
  input  [3:0] in_7,
  input  [3:0] in_8,
  input  [2:0] in_9,
  output [3:0] out_10
);

  _8x1_Multiplexer_2Bit u_8x1_multiplexer_2bit_1 (
    .in_1(in_1[1:0]), .in_2(in_2[1:0]), .in_3(in_3[1:0]), .in_4(in_4[1:0]), .in_5(in_5[1:0]),
    .in_6(in_6[1:0]), .in_7(in_7[1:0]), .in_8(in_8[1:0]), .in_9(in_9), .out_10(out_10[1:0]));
  _8x1_Multiplexer_2Bit u_8x1_multiplexer_2bit_2 (
    .in_1(in_1[3:2]), .in_2(in_2[3:2]), .in_3(in_3[3:2]), .in_4(in_4[3:2]), .in_5(in_5[3:2]),
    .in_6(in_6[3:2]), .in_7(in_7[3:2]), .in_8(in_8[3:2]), .in_9(in_9), .out_10(out_10[3:2]));
endmodule

module _8X1_Multiplexer_8Bit (
  input  [7:0] in_1,
  input  [7:0] in_2,
  input  [7:0] in_3,
  input  [7:0] in_4,
  input  [7:0] in_5,
  input  [7:0] in_6,
  input  [7:0] in_7,
  input  [7:0] in_8,
  input  [2:0] in_9,
  output [7:0] out_10
);

  _8X1_Multiplexer_4Bit u_8x1_multiplexer_4bit_1 (
    .in_1(in_1[3:0]), .in_2(in_2[3:0]), .in_3(in_3[3:0]), .in_4(in_4[3:0]), .in_5(in_5[3:0]),
    .in_6(in_6[3:0]), .in_7(in_7[3:0]), .in_8(in_8[3:0]), .in_9(in_9), .out_10(out_10[3:0]));
  _8X1_Multiplexer_4Bit u_8x1_multiplexer_4bit_2 (
    .in_1(in_1[7:4]), .in_2(in_2[7:4]), .in_3(in_3[7:4]), .in_4(in_4[7:4]), .in_5(in_5[7:4]),
    .in_6(in_6[7:4]), .in_7(in_7[7:4]), .in_8(in_8[7:4]), .in_9(in_9), .out_10(out_10[7:4]));
endmodule

module _8X1_Multiplexer_16Bit (
  input  [15:0] in_1,
  input  [15:0] in_2,
  input  [15:0] in_3,
  input  [15:0] in_4,
  input  [15:0] in_5,
  input  [15:0] in_6,
  input  [15:0] in_7,
  input  [2:0] in_8,
  input  [15:0] in_9,
  output [15:0] out_10
);

  _8X1_Multiplexer_8Bit u_8x1_multiplexer_8bit_1 (
    .in_1(in_1[7:0]), .in_2(in_2[7:0]), .in_3(in_3[7:0]), .in_4(in_4[7:0]), .in_5(in_5[7:0]),
    .in_6(in_6[7:0]), .in_7(in_7[7:0]), .in_8(in_9[7:0]), .in_9(in_8), .out_10(out_10[7:0]));
  _8X1_Multiplexer_8Bit u_8x1_multiplexer_8bit_2 (
    .in_1(in_1[15:8]), .in_2(in_2[15:8]), .in_3(in_3[15:8]), .in_4(in_4[15:8]), .in_5(in_5[15:8]),
    .in_6(in_6[15:8]), .in_7(in_7[15:8]), .in_8(in_9[15:8]), .in_9(in_8), .out_10(out_10[15:8]));
endmodule

module SRF (
  input  Reset,
  input  Clock,
  input  Set,
  output out_4,
  output out_5
);

  wire and_1_out, and_2_out, or_1_out, or_2_out;

  and and_1 (and_1_out, Reset, Clock);
  and and_2 (and_2_out, Clock, Set);
  or or_1 (or_1_out, and_1_out, out_5);
  or or_2 (or_2_out, out_4, and_2_out);
  not not_1 (out_5, or_2_out);
  not not_2 (out_4, or_1_out);
endmodule

module DFF (
  input  in_1,
  input  in_2,
  output out_3,
  output out_4
);

  wire not_1_out, not_2_out, srf_1_out_4, srf_1_out_5;

  not not_1 (not_1_out, in_1);
  SRF srf_1 (.Reset(not_1_out), .Clock(in_2), .Set(in_1), .out_4(srf_1_out_4), .out_5(srf_1_out_5));
  not not_2 (not_2_out, in_2);
  SRF srf_2 (.Reset(srf_1_out_5), .Clock(not_2_out), .Set(srf_1_out_4), .out_4(out_3), .out_5(out_4));
endmodule

module SRFF (
  input  Reset,
  input  Clock,
  input  Set,
  output out_4,
  output out_5
);

  wire and_1_out, and_2_out, or_1_out, or_2_out;

  and and_1 (and_1_out, Reset, Clock);
  and and_2 (and_2_out, Clock, Set);
  or or_1 (or_1_out, and_1_out, out_5);
  not not_1 (out_5, or_2_out);
  or or_2 (or_2_out, out_4, and_2_out);
  not not_2 (out_4, or_1_out);
endmodule

module _1Bit_Register (
  input  in_1,
  input  in_2,
  input  in_3,
  input  in_4,
  input  [2:0] C,
  output out_6,
  output out_7
);

  wire and_2_out, and_3_out, multiplexer_1_out, not_1_out, not_2_out, not_3_out, xor_1_out;
  wire [1:0] or_1_out;

  not not_1 (not_1_out, C[0]);
  not not_2 (not_2_out, C[1]);
  not not_3 (not_3_out, C[2]);
  and and_1 (or_1_out[1], not_2_out, not_3_out);
  and and_2 (and_2_out, not_1_out, not_3_out);
  and and_3 (and_3_out, not_3_out, C[1]);
  xor xor_1 (xor_1_out, in_3, out_6);
  or or_1 (or_1_out[0], and_2_out, and_3_out);
  Multiplexer #(.select(2)) multiplexer_1 (
    .in0(in_2), .in1(xor_1_out), .in2(1'b0), .in3(out_6), .out(multiplexer_1_out), .sel(or_1_out), .en(in_4));
  D_Flip_Flop d_ff_1 (.clk(in_1), .D(multiplexer_1_out), .Q(out_6), .en(in_4));  // open: Qn, preset, reset
  and and_4 (out_7, out_6, in_3);

  // Notes on the sheet:
  //   I
  //   L
endmodule

module _4_Bit_Register (
  input  in_1,
  input  [3:0] in_2,
  input  in_3,
  input  in_4,
  input  [2:0] in_5,
  output out_6,
  output [3:0] out_7
);

  wire n1bit_register_2_out_7, n1bit_register_3_out_7, n1bit_register_4_out_7;

  _1Bit_Register u_1bit_register_1 (
    .in_2(in_2[3]), .in_3(n1bit_register_2_out_7), .C(in_5), .out_6(out_7[3]), .out_7(out_6), .in_4(in_3),
    .in_1(in_1));
  _1Bit_Register u_1bit_register_2 (
    .in_2(in_2[2]), .in_3(n1bit_register_3_out_7), .C(in_5), .out_6(out_7[2]),
    .out_7(n1bit_register_2_out_7), .in_4(in_3), .in_1(in_1));
  _1Bit_Register u_1bit_register_3 (
    .in_2(in_2[1]), .in_3(n1bit_register_4_out_7), .C(in_5), .out_6(out_7[1]),
    .out_7(n1bit_register_3_out_7), .in_4(in_3), .in_1(in_1));
  _1Bit_Register u_1bit_register_4 (
    .in_2(in_2[0]), .in_3(in_4), .C(in_5), .out_6(out_7[0]), .out_7(n1bit_register_4_out_7), .in_4(in_3),
    .in_1(in_1));
endmodule

module Bus (
  input  [3:0] in_1,
  input  [1:0] in_2,
  input  [1:0] in_3,
  input  [2:0] in_4,
  input  [2:0] in_5,
  input  [2:0] in_6,
  input  [2:0] in_7,
  input  in_8
);

  wire clock_1_out;
  wire [3:0] demultiplexer_1_out0, demultiplexer_1_out1, demultiplexer_1_out2, demultiplexer_1_out3,
       multiplexer_1_out, n4_bit_register_1_out_7, n4_bit_register_2_out_7, n4_bit_register_3_out_7,
       n4_bit_register_4_out_7;

  Clock clock_1 (.out(clock_1_out));
  _4_Bit_Register u_4_bit_register_1 (
    .in_1(clock_1_out), .in_3(in_8), .in_5(in_4), .out_7(n4_bit_register_1_out_7),
    .in_2(demultiplexer_1_out0), .in_4(clock_1_out));  // open: out_6
  _4_Bit_Register u_4_bit_register_2 (
    .in_1(clock_1_out), .in_3(in_8), .in_5(in_5), .out_7(n4_bit_register_2_out_7),
    .in_2(demultiplexer_1_out1), .in_4(in_8));  // open: out_6
  _4_Bit_Register u_4_bit_register_3 (
    .in_1(clock_1_out), .in_5(in_6), .out_7(n4_bit_register_3_out_7), .in_2(demultiplexer_1_out2), .in_4(in_8));  // open: in_3, out_6
  _4_Bit_Register u_4_bit_register_4 (
    .in_1(clock_1_out), .in_3(in_8), .in_5(in_7), .out_7(n4_bit_register_4_out_7),
    .in_2(demultiplexer_1_out3), .in_4(in_8));  // open: out_6
  Multiplexer #(.select(2), .width(4)) multiplexer_1 (
    .in0(n4_bit_register_1_out_7), .in1(n4_bit_register_2_out_7), .in2(n4_bit_register_3_out_7),
    .in3(n4_bit_register_4_out_7), .out(multiplexer_1_out), .sel(in_2), .en(in_8));
  Demultiplexer #(.select(2), .width(4)) demultiplexer_1 (
    .out0(demultiplexer_1_out0), .out1(demultiplexer_1_out1), .out2(demultiplexer_1_out2),
    .out3(demultiplexer_1_out3), .in(multiplexer_1_out), .sel(in_3), .en(in_8));
endmodule

module Binary_Adder_Subtractor (
  input  [3:0] in_1,
  input  [3:0] in_2,
  input  in_3,
  output out_4,
  output [3:0] out_5
);

  wire full_adder_2_cn, full_adder_3_cn, full_adder_4_cn;

  Full_Adder full_adder_1 (.X(in_1[3]), .Y(in_2[3]), .Cn_1(full_adder_2_cn), .S(out_5[3]), .Cn(out_4));
  Full_Adder full_adder_2 (.X(in_1[2]), .Y(in_2[2]), .Cn_1(full_adder_3_cn), .S(out_5[2]), .Cn(full_adder_2_cn));
  Full_Adder full_adder_3 (.X(in_1[1]), .Y(in_2[1]), .Cn_1(full_adder_4_cn), .S(out_5[1]), .Cn(full_adder_3_cn));
  Full_Adder full_adder_4 (.X(in_1[0]), .Y(in_2[0]), .Cn_1(in_3), .S(out_5[0]), .Cn(full_adder_4_cn));
endmodule

module _1Bit_AU (
  input  in_1,
  input  in_2,
  input  in_3,
  input  [1:0] in_4,
  output out_5,
  output out_6
);

  wire n4x1multiplexer_1_out_6, not_1_out, not_2_out;

  not not_1 (not_1_out, in_3);
  not not_2 (not_2_out, 1'b0);
  _4X1Multiplexer u_4x1multiplexer_1 (
    .in_1(in_3), .in_2(not_1_out), .in_3(1'b0), .in_4(not_2_out), .out_6(n4x1multiplexer_1_out_6), .in_5(in_4));
  Full_Adder full_adder_1 (.X(in_2), .Y(n4x1multiplexer_1_out_6), .Cn_1(in_1), .S(out_5), .Cn(out_6));
endmodule

module _1Bit_AU_2 (
  input  in_1,
  input  in_2,
  input  in_3,
  input  [1:0] in_4,
  output out_5,
  output out_6
);

  wire n4x1multiplexer_1_out_6, not_1_out, not_2_out;

  not not_1 (not_1_out, in_3);
  not not_2 (not_2_out, 1'b0);
  _4X1Multiplexer u_4x1multiplexer_1 (
    .in_1(1'b0), .in_2(in_3), .in_3(not_1_out), .in_4(not_2_out), .out_6(n4x1multiplexer_1_out_6), .in_5(in_4));
  Full_Adder full_adder_1 (.X(in_2), .Y(n4x1multiplexer_1_out_6), .Cn_1(in_1), .S(out_5), .Cn(out_6));
endmodule

module _4Bit_AU (
  input  [3:0] in_1,
  input  in_2,
  input  [3:0] in_3,
  input  [1:0] in_4,
  output [3:0] out_5,
  output out_6
);

  wire n1bit_au_1_out_6, n1bit_au_2_out_6, n1bit_au_3_out_6;

  _1Bit_AU_2 u_1bit_au_1 (
    .in_1(in_2), .in_2(in_1[0]), .in_3(in_3[0]), .in_4(in_4), .out_5(out_5[0]), .out_6(n1bit_au_1_out_6));
  _1Bit_AU_2 u_1bit_au_2 (
    .in_1(n1bit_au_1_out_6), .in_2(in_1[1]), .in_3(in_3[1]), .in_4(in_4), .out_5(out_5[1]),
    .out_6(n1bit_au_2_out_6));
  _1Bit_AU_2 u_1bit_au_3 (
    .in_1(n1bit_au_2_out_6), .in_2(in_1[2]), .in_3(in_3[2]), .in_4(in_4), .out_5(out_5[2]),
    .out_6(n1bit_au_3_out_6));
  _1Bit_AU_2 u_1bit_au_4 (
    .in_1(n1bit_au_3_out_6), .in_2(in_1[3]), .in_3(in_3[3]), .in_4(in_4), .out_5(out_5[3]), .out_6(out_6));
endmodule

module _1_Bit_LU (
  input  in_1,
  input  in_2,
  input  in_3,
  input  [1:0] in_4,
  output out_5
);

  wire and_1_out, not_1_out, not_2_out, not_3_out, not_4_out, or_1_out, xor_1_out;

  and and_1 (and_1_out, in_1, in_2);
  or or_1 (or_1_out, in_1, in_2);
  xor xor_1 (xor_1_out, in_1, in_2);
  not not_1 (not_1_out, in_1);
  not not_2 (not_2_out, and_1_out);
  not not_3 (not_3_out, or_1_out);
  not not_4 (not_4_out, xor_1_out);
  _8X1_Multiplexer u_8x1_multiplexer_1 (
    .in_1(and_1_out), .in_2(not_2_out), .in_3(not_3_out), .in_4(not_4_out), .in_5(or_1_out),
    .in_6(xor_1_out), .in_7(not_1_out), .in_8(not_1_out), .in_9({in_4, in_3}), .out_10(out_5));
endmodule

module _4_Bit_LU (
  input  [3:0] in_1,
  input  in_2,
  input  [3:0] in_3,
  input  [1:0] in_4,
  output [3:0] out_5
);

  _1_Bit_LU u_1_bit_lu_1 (.in_1(in_1[0]), .in_2(in_3[0]), .out_5(out_5[0]), .in_3(in_2), .in_4(in_4));
  _1_Bit_LU u_1_bit_lu_2 (.in_1(in_1[1]), .in_2(in_3[1]), .out_5(out_5[1]), .in_3(in_2), .in_4(in_4));
  _1_Bit_LU u_1_bit_lu_3 (.in_1(in_1[2]), .in_2(in_3[2]), .out_5(out_5[2]), .in_3(in_2), .in_4(in_4));
  _1_Bit_LU u_1_bit_lu_4 (.in_1(in_1[3]), .in_2(in_3[3]), .out_5(out_5[3]), .in_3(in_2), .in_4(in_4));
endmodule

module _16_Bit_LU (
  input  [15:0] in_1,
  input  in_2,
  input  [15:0] in_3,
  input  [1:0] in_4,
  output [15:0] out_5
);

  _4_Bit_LU u_4_bit_lu_1 (.in_1(in_1[3:0]), .in_2(in_2), .in_3(in_3[3:0]), .in_4(in_4), .out_5(out_5[3:0]));
  _4_Bit_LU u_4_bit_lu_2 (.in_1(in_1[7:4]), .in_2(in_2), .in_3(in_3[7:4]), .in_4(in_4), .out_5(out_5[7:4]));
  _4_Bit_LU u_4_bit_lu_3 (.in_1(in_1[11:8]), .in_2(in_2), .in_3(in_3[11:8]), .in_4(in_4), .out_5(out_5[11:8]));
  _4_Bit_LU u_4_bit_lu_4 (.in_1(in_1[15:12]), .in_2(in_2), .in_3(in_3[15:12]), .in_4(in_4), .out_5(out_5[15:12]));
endmodule

module _4_Bit_SU (
  input  in_1,
  input  in_2,
  input  [3:0] in_3,
  input  in_4,
  input  in_5,
  output out_6,
  output [3:0] out_7,
  output out_8
);

  wire not_1_out;

  not not_1 (not_1_out, in_4);
  Multiplexer multiplexer_1 (.in0(in_3[3]), .out(out_6), .sel(not_1_out), .en(in_5));  // open: in1
  Multiplexer multiplexer_2 (.in0(in_3[2]), .in1(in_1), .out(out_7[3]), .sel(not_1_out), .en(in_5));
  Multiplexer multiplexer_3 (.in0(in_3[1]), .in1(in_3[3]), .out(out_7[2]), .sel(not_1_out), .en(in_5));
  Multiplexer multiplexer_4 (.in0(in_3[0]), .in1(in_3[2]), .out(out_7[1]), .sel(not_1_out), .en(in_5));
  Multiplexer multiplexer_5 (.in0(in_2), .in1(in_3[1]), .out(out_7[0]), .sel(not_1_out), .en(in_5));
  Multiplexer multiplexer_6 (.in1(in_3[0]), .out(out_8), .sel(not_1_out), .en(in_5));  // open: in0
endmodule

module _16_Bit_AU (
  input  [15:0] in_1,
  input  in_2,
  input  [15:0] in_3,
  input  [1:0] in_4,
  output [15:0] out_5,
  output out_6
);

  wire n4bit_au_1_out_6, n4bit_au_2_out_6, n4bit_au_3_out_6;

  _4Bit_AU u_4bit_au_1 (
    .in_1(in_1[3:0]), .in_2(in_2), .in_3(in_3[3:0]), .in_4(in_4), .out_5(out_5[3:0]), .out_6(n4bit_au_1_out_6));
  _4Bit_AU u_4bit_au_2 (
    .in_1(in_1[7:4]), .in_2(n4bit_au_1_out_6), .in_3(in_3[7:4]), .in_4(in_4), .out_5(out_5[7:4]),
    .out_6(n4bit_au_2_out_6));
  _4Bit_AU u_4bit_au_3 (
    .in_1(in_1[11:8]), .in_2(n4bit_au_2_out_6), .in_3(in_3[11:8]), .in_4(in_4), .out_5(out_5[11:8]),
    .out_6(n4bit_au_3_out_6));
  _4Bit_AU u_4bit_au_4 (
    .in_1(in_1[15:12]), .in_2(n4bit_au_3_out_6), .in_3(in_3[15:12]), .in_4(in_4), .out_5(out_5[15:12]),
    .out_6(out_6));
endmodule

module _16_Bit_ALSU (
  input  [15:0] in_1,
  input  [15:0] in_2,
  input  in_3,
  input  in_4,
  input  [3:0] in_5,
  output [15:0] out_6,
  output out_7,
  output out_8,
  output out_9
);

  wire [15:0] n16_bit_au_1_out_5, n16_bit_lu_1_out_5, n16_bit_su_1_out_4;

  _16_Bit_SU u_16_bit_su_1 (
    .in_1(in_1), .in_2(in_3), .out_4(n16_bit_su_1_out_4), .out_5(out_8), .in_3({in_5[3:2], in_4}));
  _16_Bit_LU u_16_bit_lu_1 (.in_1(in_1), .in_2(in_4), .in_3(in_2), .in_4(in_5[1:0]), .out_5(n16_bit_lu_1_out_5));
  _16_Bit_AU u_16_bit_au_1 (
    .in_1(in_1), .in_2(in_4), .in_3(in_2), .in_4(in_5[1:0]), .out_5(n16_bit_au_1_out_5), .out_6(out_9));
  Multiplexer #(.select(2), .width(16)) multiplexer_1 (
    .in0(n16_bit_su_1_out_4), .in1(n16_bit_lu_1_out_5), .in2(n16_bit_au_1_out_5), .in3(n16_bit_au_1_out_5),
    .out({out_6[15:10], out_6[10], out_6[8:0]}), .sel(in_5[3:2]), .en(in_3));
  nor nor_1 (out_7, out_6[0], out_6[1], out_6[2], out_6[3], out_6[4], out_6[5], out_6[6], out_6[7], out_6[8], out_6[10], out_6[10], out_6[11], out_6[12], out_6[13], out_6[14], out_6[15]);

  assign out_6[9] = out_6[10];
endmodule

module _16_Bit_SU (
  input  [15:0] in_1,
  input  in_2,
  input  [2:0] in_3,
  output [15:0] out_4,
  output out_5
);

  wire and_1_out, and_2_out, and_3_out, multiplexer_1_out, multiplexer_2_out, n4_bit_su_1_out_6,
       n4_bit_su_1_out_8, n4_bit_su_2_out_6, n4_bit_su_2_out_8, n4_bit_su_3_out_6, n4_bit_su_3_out_8,
       n4_bit_su_4_out_6, n4_bit_su_4_out_8, not_1_out, not_2_out, not_3_out, or_1_out, xor_1_out;

  _4_Bit_SU u_4_bit_su_1 (
    .in_3(in_1[15:12]), .out_7(out_4[15:12]), .out_8(n4_bit_su_1_out_8), .in_1(multiplexer_1_out),
    .in_2(n4_bit_su_2_out_6), .in_4(or_1_out), .in_5(in_2), .out_6(n4_bit_su_1_out_6));
  Multiplexer #(.select(3)) multiplexer_1 (
    .in0(1'b0), .in1(in_1[15]), .in2(n4_bit_su_4_out_8), .out(multiplexer_1_out), .sel(in_3), .en(in_2));  // open: in3, in4, in5, in6, in7
  and and_1 (and_1_out, in_3[2], not_2_out);
  xor xor_1 (xor_1_out, in_1[15], in_1[14]);
  _4_Bit_SU u_4_bit_su_2 (
    .in_3(in_1[11:8]), .out_7(out_4[11:8]), .out_8(n4_bit_su_2_out_8), .in_1(n4_bit_su_1_out_8),
    .in_2(n4_bit_su_3_out_6), .in_4(or_1_out), .in_5(in_2), .out_6(n4_bit_su_2_out_6));
  or or_1 (or_1_out, and_1_out, and_2_out, and_3_out);
  and and_2 (and_2_out, in_3[2], not_1_out);
  not not_1 (not_1_out, in_3[1]);
  not not_2 (not_2_out, in_3[0]);
  and and_3 (and_3_out, not_3_out, in_3[1], in_3[0]);
  not not_3 (not_3_out, in_3[2]);
  _4_Bit_SU u_4_bit_su_3 (
    .in_3(in_1[7:4]), .out_7(out_4[7:4]), .out_8(n4_bit_su_3_out_8), .in_1(n4_bit_su_2_out_8),
    .in_2(n4_bit_su_4_out_6), .in_4(or_1_out), .in_5(in_2), .out_6(n4_bit_su_3_out_6));
  _4_Bit_SU u_4_bit_su_4 (
    .in_3(in_1[3:0]), .out_7(out_4[3:0]), .out_8(n4_bit_su_4_out_8), .in_1(n4_bit_su_3_out_8),
    .in_2(multiplexer_2_out), .in_4(or_1_out), .in_5(in_2), .out_6(n4_bit_su_4_out_6));
  Multiplexer #(.select(3)) multiplexer_2 (
    .in3(1'b0), .in4(1'b0), .in5(n4_bit_su_1_out_6), .in6(1'b0), .out(multiplexer_2_out), .sel(in_3),
    .en(in_2));  // open: in0, in1, in2, in7
  Multiplexer #(.select(3)) multiplexer_3 (
    .in0(1'b0), .in1(1'b0), .in2(1'b0), .in3(1'b0), .in4(xor_1_out), .in5(1'b0), .in6(xor_1_out), .in7(1'b0),
    .out(out_5), .sel(in_3), .en(in_2));
endmodule
