// Logisim project MicroProgramedComputer.circ as structural Verilog: 9 circuits, main circuit main
module Control_Unit (
  input  in_1,
  input  E,
  input  [15:0] in_3,
  input  [15:0] in_4,
  output F3_1,
  output F3_5,
  output F3_2,
  output F3_6,
  output F3_3,
  output F3_7,
  output F3_4,
  output F3_8,
  output F2_1,
  output F2_5,
  output F2_2,
  output F2_6,
  output F2_3,
  output F2_7,
  output F2_4,
  output F2_8,
  output F1_1,
  output F1_5,
  output F1_2,
  output F1_6,
  output F1_3,
  output F1_7,
  output F1_4,
  output F1_8
);

  wire AC_0, L, multiplexer_1_out, or_1_out;
  wire [1:0] BR, CD, S1S0;
  wire [6:0] _0_6, CAR_out_6, Incrementer, multiplexer_2_out, SBR;
  wire [19:11] rom_1_data;

  Multiplexer #(.select(2)) multiplexer_1 (
    .in0(1'b1), .in1(in_3[15]), .in2(in_4[15]), .in3(AC_0), .out(multiplexer_1_out), .sel(CD), .en(E));
  or or_1 (or_1_out, in_4[0], in_4[1], in_4[2], in_4[3], in_4[4], in_4[5], in_4[6], in_4[7], in_4[8], in_4[9], in_4[10], in_4[11], in_4[12], in_4[13], in_4[14], in_4[15]);
  Multiplexer #(.select(2), .width(7)) multiplexer_2 (
    .in0(Incrementer), .in1(SBR), .in2(_0_6), .in3({1'b0, in_3[14:11], 2'b00}), .out(multiplexer_2_out),
    .sel(S1S0), .en(E));
  inputLogic inputlogic_1 (.T(multiplexer_1_out), .I1(BR[1]), .I0(BR[0]), .L(L), .S0(S1S0[0]), .S1(S1S0[1]));
  not not_1 (AC_0, or_1_out);
  _7_Bit_Register CAR (
    .in_1(in_1), .out_6(CAR_out_6), .in_2(multiplexer_2_out), .in_3(3'b111), .in_4(E));  // open: out_5
  Adder #(.width(7)) adder_1 (.a(CAR_out_6), .b(7'b0000001), .out(Incrementer));  // open: cin, cout
  ROM #(.addrWidth(7), .dataWidth(20)) rom_1 (.addr(CAR_out_6), .data({rom_1_data, CD, BR, _0_6}), .sel(E));
  _7_Bit_Register u_SBR (.in_1(in_1), .out_6(SBR), .in_2(Incrementer), .in_3({L, 2'b00}), .in_4(E));  // open: out_5
  Decoder #(.select(3)) decoder_1 (
    .out0(F3_1), .out1(F3_2), .out2(F3_3), .out3(F3_4), .out4(F3_5), .out5(F3_6), .out6(F3_7), .out7(F3_8),
    .sel(rom_1_data[13:11]), .en(E));
  Decoder #(.select(3)) decoder_2 (
    .out0(F2_1), .out1(F2_2), .out2(F2_3), .out3(F2_4), .out4(F2_5), .out5(F2_6), .out6(F2_7), .out7(F2_8),
    .sel(rom_1_data[16:14]), .en(E));
  Decoder #(.select(3)) decoder_3 (
    .out0(F1_1), .out1(F1_2), .out2(F1_3), .out3(F1_4), .out4(F1_5), .out5(F1_6), .out6(F1_7), .out7(F1_8),
    .sel(rom_1_data[19:17]), .en(E));

  // Other names for the same wires on the sheet: Clock = in_1; AC_15 = in_4[15]

  // Notes on the sheet:
  //   contents of rom_1 (hex, n*v repeats v):
  //   1f3
endmodule

module main (
  input  E
);

  wire Clock, control_unit_1_f1_6, control_unit_1_f1_7;
  wire [2:0] AR_C;
  wire [3:0] control_unit_1_f2_4;
  wire [10:0] AB, AR, bit_extender_1_out, PC;
  wire [15:0] AC, alu16_1_out_6, bit_extender_2_out, DR, M, multiplexer_2_out;

  Clock clock_1 (.out(Clock));
  Bit_Extender #(.in_width(16), .out_width(11)) bit_extender_1 (.in(DR), .out(bit_extender_1_out));
  // OR_Gate or_1 has open pins: in0=control_unit_1_f1_6, in1=control_unit_1_f1_7, out=open
  Multiplexer #(.width(11)) multiplexer_1 (
    .in0(PC), .in1(bit_extender_1_out), .out(AB), .sel(control_unit_1_f1_6), .en(E));
  RAM #(.addrWidth(11), .dataWidth(16), .bus("separate")) ram_1 (
    .addr(AR), .din(DR), .data(M), .clk(Clock));  // open: str, sel, ld, clr
  _11_Bit_Register u_AR (.in_1(Clock), .out_6(AR), .in_2(AB), .in_3(AR_C), .in_4(E));  // open: out_5
  assign bit_extender_2_out = {{5{1'b0}}, PC};  // Bit_Extender bit_extender_2
  _11_Bit_Register u_PC (.in_1(Clock), .out_6(PC), .in_2(AR), .in_4(E));  // open: out_5, in_3
  Multiplexer #(.select(2), .width(16)) multiplexer_2 (
    .in0(AC), .in1(bit_extender_2_out), .in2(M), .out(multiplexer_2_out), .en(E));  // open: in3, sel
  _16_Bit_Register u_DR (.out_6(DR), .in_1(Clock), .in_2(multiplexer_2_out), .in_3(E));  // open: out_5, in_4
  Control_Unit control_unit_1 (
    .in_3(DR), .E(E), .in_4(AC), .in_1(Clock), .F2_4(control_unit_1_f2_4[0]), .F1_2(control_unit_1_f2_4[1]),
    .F1_4(control_unit_1_f2_4[2]), .F1_6(control_unit_1_f1_6), .F1_7(control_unit_1_f1_7));  // open: F3_3, F3_2, F3_1, F3_4, F3_5, F3_6, F3_7, F3_8, F2_1, F2_2, F2_3, F2_5, F2_6, F2_7, F2_8, F1_1, F1_3, F1_5, F1_8
  ALU16 alu16_1 (
    .in_3(E), .in_4(DR), .in_5(AC), .out_6(alu16_1_out_6), .in_2(control_unit_1_f2_4));  // open: in_1, out_7
  _16_Bit_Register u_AC (.out_6(AC), .in_1(Clock), .in_2(alu16_1_out_6), .in_3(E));  // open: out_5, in_4
endmodule

module AU16B (
  input  in_1,
  input  [15:0] in_2,
  input  [15:0] in_3,
  input  [1:0] in_4,
  input  in_5,
  output [15:0] out_6,
  output out_7
);

  wire [15:0] multiplexer_1_out, not_1_out;

  assign not_1_out = ~in_3;  // NOT_Gate not_1, 16 bits wide
  Multiplexer #(.select(2), .width(16)) multiplexer_1 (
    .in0(in_3), .in1(not_1_out), .in2({16{1'b0}}), .in3(16'h1), .out(multiplexer_1_out), .sel(in_4), .en(in_5));
  Adder #(.width(16)) adder_1 (.a(in_2), .b(multiplexer_1_out), .out(out_6), .cin(in_1), .cout(out_7));
endmodule

module LU16B (
  input  [15:0] in_1,
  input  [15:0] in_2,
  input  [1:0] in_3,
  input  in_4,
  output [15:0] out_5
);

  wire [15:0] and_1_out, not_1_out, or_1_out, xor_1_out;

  assign and_1_out = in_1 & in_2;  // AND_Gate and_1, 16 bits wide
  assign or_1_out = in_1 | in_2;  // OR_Gate or_1, 16 bits wide
  assign xor_1_out = in_1 ^ in_2;  // XOR_Gate xor_1, 16 bits wide
  assign not_1_out = ~in_1;  // NOT_Gate not_1, 16 bits wide
  Multiplexer #(.select(2), .width(16)) multiplexer_1 (
    .in0(and_1_out), .in1(or_1_out), .in2(xor_1_out), .in3(not_1_out), .out(out_5), .sel(in_3), .en(in_4));
endmodule

module ALU16 (
  input  in_1,
  input  [3:0] in_2,
  input  in_3,
  input  [15:0] in_4,
  input  [15:0] in_5,
  output [15:0] out_6,
  output out_7
);

  wire [15:0] au16b_1_out_6, demultiplexer_1_out0, demultiplexer_1_out1, lu16b_1_out_5, n16su_1_out_6;

  AU16B au16b_1 (
    .in_1(in_1), .in_2(in_4), .in_3(in_5), .in_4(in_2[1:0]), .in_5(in_3), .out_6(au16b_1_out_6), .out_7(out_7));
  LU16B lu16b_1 (.in_1(in_4), .in_2(in_5), .in_3(in_2[1:0]), .in_4(in_3), .out_5(lu16b_1_out_5));
  _16SU u_16su_1 (
    .in_1(in_4), .out_6(n16su_1_out_6), .in_2(in_3), .in_5(in_2[2]), .in_4(1'b0), .in_3(1'b0));  // open: out_7, out_8
  Demultiplexer #(.width(16)) demultiplexer_1 (
    .out0(demultiplexer_1_out0), .out1(demultiplexer_1_out1), .in(n16su_1_out_6), .sel(in_2[2]), .en(in_3));
  Multiplexer #(.select(2), .width(16)) multiplexer_1 (
    .in0(au16b_1_out_6), .in1(lu16b_1_out_5), .in2(demultiplexer_1_out0), .in3(demultiplexer_1_out1),
    .out(out_6), .sel(in_2[3:2]), .en(in_3));
endmodule

module _16SU (
  input  [15:0] in_1,
  input  in_2,
  input  in_3,
  input  in_4,
  input  in_5,
  output [15:0] out_6,
  output out_7,
  output out_8
);

  wire n4_bit_su_1_out_8, n4_bit_su_2_out_6, n4_bit_su_2_out_8, n4_bit_su_3_out_6, n4_bit_su_3_out_8,
       n4_bit_su_4_out_6;

  _4_Bit_SU u_4_bit_su_1 (
    .in_1(in_4), .out_6(out_7), .out_7(out_6[15:12]), .out_8(n4_bit_su_1_out_8), .in_2(in_1[15:12]),
    .in_5(in_2), .in_3(n4_bit_su_2_out_6), .in_4(in_5));
  _4_Bit_SU u_4_bit_su_2 (
    .in_1(n4_bit_su_1_out_8), .out_6(n4_bit_su_2_out_6), .out_7(out_6[11:8]), .out_8(n4_bit_su_2_out_8),
    .in_2(in_1[11:8]), .in_5(in_2), .in_3(n4_bit_su_3_out_6), .in_4(in_5));
  _4_Bit_SU u_4_bit_su_3 (
    .in_1(n4_bit_su_2_out_8), .out_6(n4_bit_su_3_out_6), .out_7(out_6[7:4]), .out_8(n4_bit_su_3_out_8),
    .in_2(in_1[7:4]), .in_5(in_2), .in_3(n4_bit_su_4_out_6), .in_4(in_5));
  _4_Bit_SU u_4_bit_su_4 (
    .in_1(n4_bit_su_3_out_8), .out_6(n4_bit_su_4_out_6), .out_7(out_6[3:0]), .out_8(out_8), .in_2(in_1[3:0]),
    .in_5(in_2), .in_3(in_3), .in_4(in_5));
endmodule

module _11_Bit_Register (
  input  in_1,
  input  [10:0] in_2,
  input  [2:0] in_3,
  input  in_4,
  output out_5,
  output [10:0] out_6
);

  wire n1_bit_register_2_out_7, n1_bit_register_3_out_7, n4_bit_register_1_out_6, n4_bit_register_2_out_6;

  _1_Bit_Register u_1_bit_register_1 (
    .in_2(in_2[10]), .in_3(n1_bit_register_2_out_7), .out_6(out_6[10]), .in_4(in_4), .out_7(out_5),
    .in_5(in_3), .in_1(in_1));
  _1_Bit_Register u_1_bit_register_2 (
    .in_2(in_2[9]), .in_3(n1_bit_register_3_out_7), .out_6(out_6[9]), .in_4(in_4),
    .out_7(n1_bit_register_2_out_7), .in_5(in_3), .in_1(in_1));
  _1_Bit_Register u_1_bit_register_3 (
    .in_2(in_2[8]), .in_3(n4_bit_register_1_out_6), .out_6(out_6[8]), .in_4(in_4),
    .out_7(n1_bit_register_3_out_7), .in_5(in_3), .in_1(in_1));
  _4_Bit_Register u_4_bit_register_1 (
    .out_6(n4_bit_register_1_out_6), .out_7(out_6[7:4]), .in_2(in_2[7:4]), .in_4(in_4), .in_3(in_3),
    .in_5(n4_bit_register_2_out_6), .in_1(in_1));
  _4_Bit_Register u_4_bit_register_2 (
    .out_6(n4_bit_register_2_out_6), .out_7(out_6[3:0]), .in_2(in_2[3:0]), .in_4(in_4), .in_3(in_3),
    .in_5(1'b1), .in_1(in_1));
endmodule

module _7_Bit_Register (
  input  in_1,
  input  [6:0] in_2,
  input  [2:0] in_3,
  input  in_4,
  output out_5,
  output [6:0] out_6
);

  wire n1_bit_register_2_out_7, n1_bit_register_3_out_7, n4_bit_register_1_out_6;

  _1_Bit_Register u_1_bit_register_1 (
    .in_2(in_2[6]), .in_3(n1_bit_register_2_out_7), .out_6(out_6[6]), .in_4(in_4), .out_7(out_5),
    .in_5(in_3), .in_1(in_1));
  _1_Bit_Register u_1_bit_register_2 (
    .in_2(in_2[5]), .in_3(n1_bit_register_3_out_7), .out_6(out_6[5]), .in_4(in_4),
    .out_7(n1_bit_register_2_out_7), .in_5(in_3), .in_1(in_1));
  _1_Bit_Register u_1_bit_register_3 (
    .in_2(in_2[4]), .in_3(n4_bit_register_1_out_6), .out_6(out_6[4]), .in_4(in_4),
    .out_7(n1_bit_register_3_out_7), .in_5(in_3), .in_1(in_1));
  _4_Bit_Register u_4_bit_register_1 (
    .out_6(n4_bit_register_1_out_6), .out_7(out_6[3:0]), .in_2(in_2[3:0]), .in_4(in_4), .in_3(in_3),
    .in_5(1'b1), .in_1(in_1));
endmodule

module inputLogic (
  input  T,
  input  I1,
  input  I0,
  output L,
  output S0,
  output S1
);

  wire and_1_out, and_2_out, not_1_out, not_2_out;

  not not_1 (not_1_out, I0);
  and and_1 (and_1_out, T, not_1_out);
  or or_1 (S1, and_1_out, and_2_out);
  and and_2 (and_2_out, I1, I0);
  not not_2 (not_2_out, I0);
  and and_3 (L, I1, T, not_2_out);

  assign S0 = I0;
endmodule
