// Logisim project My4x1_AU.circ as structural Verilog: 1 circuit, main circuit main
module main (
  input  in_1,
  input  [3:0] in_2,
  input  [1:0] in_3,
  input  in_4,
  input  [3:0] in_5,
  output [3:0] out_6,
  output out_7
);

  wire adder_1_cout, adder_2_cout, adder_3_cout, multiplexer_1_out, multiplexer_2_out, multiplexer_3_out,
       multiplexer_4_out, not_1_out, not_2_out, not_3_out, not_4_out, not_5_out;

  not not_1 (not_1_out, in_5[0]);
  not not_2 (not_2_out, in_5[1]);
  not not_3 (not_3_out, in_5[2]);
  not not_4 (not_4_out, in_5[3]);
  not not_5 (not_5_out, 1'b0);
  Multiplexer #(.select(2)) multiplexer_1 (
    .in0(in_5[0]), .in1(not_1_out), .in2(1'b0), .in3(not_5_out), .out(multiplexer_1_out), .sel(in_3),
    .en(in_4));
  Multiplexer #(.select(2)) multiplexer_2 (
    .in0(in_5[1]), .in1(not_2_out), .in2(1'b0), .in3(not_5_out), .out(multiplexer_2_out), .sel(in_3),
    .en(in_4));
  Multiplexer #(.select(2)) multiplexer_3 (
    .in0(in_5[2]), .in1(not_3_out), .in2(1'b0), .in3(not_5_out), .out(multiplexer_3_out), .sel(in_3),
    .en(in_4));
  Multiplexer #(.select(2)) multiplexer_4 (
    .in0(in_5[3]), .in1(not_4_out), .in2(1'b0), .in3(not_5_out), .out(multiplexer_4_out), .sel(in_3),
    .en(in_4));
  Adder #(.width(1)) adder_1 (.a(in_2[0]), .b(multiplexer_1_out), .out(out_6[0]), .cin(in_1), .cout(adder_1_cout));
  Adder #(.width(1)) adder_2 (
    .a(in_2[1]), .b(multiplexer_2_out), .out(out_6[1]), .cin(adder_1_cout), .cout(adder_2_cout));
  Adder #(.width(1)) adder_3 (
    .a(in_2[2]), .b(multiplexer_3_out), .out(out_6[2]), .cin(adder_2_cout), .cout(adder_3_cout));
  Adder #(.width(1)) adder_4 (.a(in_2[3]), .b(multiplexer_4_out), .out(out_6[3]), .cin(adder_3_cout), .cout(out_7));
endmodule
