// Logisim project donanım dersi.circ as structural Verilog: 5 circuits, main circuit main
module main (
  input  in_1,
  input  in_2,
  output [1:0] out_3
);

  wire and_1_out, clock_1_out;

  Clock clock_1 (.out(clock_1_out));
  and and_1 (and_1_out, in_1, out_3[0]);
  J_K_Flip_Flop A (
    .J(and_1_out), .clk(clock_1_out), .K(and_1_out), .Q(out_3[1]), .en(in_2));  // open: Qn, preset, reset
  J_K_Flip_Flop B (.J(in_1), .clk(clock_1_out), .K(in_1), .Q(out_3[0]), .en(in_2));  // open: Qn, preset, reset
  _7_Segment_Display u_7_segment_display_1 ();  // open: g, f, a, b, e, d, c, dp
  Hex_Digit_Display hex_digit_display_1 ();  // open: value, dp
endmodule

module HA (
  input  in_1,
  input  in_2,
  output out_3,
  output out_4
);

  xor xor_1 (out_3, in_1, in_2);
  and and_1 (out_4, in_2, in_1);
endmodule

module FA (
  input  in_1,
  input  in_2,
  input  in_3,
  output out_4,
  output out_5
);

  wire ha_1_out_3, ha_1_out_4, ha_2_out_4;

  HA ha_1 (.in_1(in_1), .in_2(in_2), .out_3(ha_1_out_3), .out_4(ha_1_out_4));
  HA ha_2 (.in_1(ha_1_out_3), .in_2(in_3), .out_3(out_4), .out_4(ha_2_out_4));
  or or_1 (out_5, ha_2_out_4, ha_1_out_4);
endmodule

module RS (
  input  in_1,
  input  in_2,
  input  in_3,
  output out_4,
  output out_5
);

  wire and_1_out, and_2_out, or_1_out, or_2_out;

  and and_1 (and_1_out, in_1, in_2);
  and and_2 (and_2_out, in_2, in_3);
  or or_1 (or_1_out, and_1_out, out_5);
  or or_2 (or_2_out, out_4, and_2_out);
  not not_1 (out_4, or_1_out);
  not not_2 (out_5, or_2_out);
endmodule

module D (
  input  in_1,
  input  in_2,
  output out_3,
  output out_4
);

  wire not_1_out, not_2_out, rs_1_out_4, rs_1_out_5;

  not not_1 (not_1_out, in_2);
  not not_2 (not_2_out, in_1);
  RS rs_1 (.in_1(not_1_out), .in_2(not_2_out), .in_3(in_2), .out_4(rs_1_out_4), .out_5(rs_1_out_5));
  RS rs_2 (.in_1(rs_1_out_5), .in_2(in_1), .in_3(rs_1_out_4), .out_4(out_3), .out_5(out_4));
endmodule
